// Logisim project branch_predictor.circ as structural Verilog: 41 circuits, main circuit core
module core (
  input  clk,
  input  rst
);

  wire alu_v1_1_branch_result, and_1_out, and_2_out, C, control_unit_ew_stage2_1_data_wb_or_load,
       control_unit_ew_stage2_1_funct3_sel, control_unit_ew_stage2_1_funct_7,
       control_unit_ew_stage2_1_mem_wr_en_cntrl, control_unit_ew_stage2_1_opcode_a_sel_pc_or_reg,
       control_unit_ew_stage2_1_opcode_b_sel_reg_or_imm, control_unit_ew_stage2_1_rd_in_commit,
       control_unit_ew_stage2_1_s2_br_inst, op_fwd_check_1_rs1_s1_dep_detected,
       op_fwd_check_1_rs1_s2_dep_detected, op_fwd_check_1_rs2_s2_dep_detected, op_fwd_check_1_rs2_store_fwd,
       register_3_q, undriven_2, undriven_4, undriven_10;
  wire [1:0] undriven_3, undriven_5;
  wire [2:0] control_unit_ew_stage2_1_mem_strobe, inter_stage_buffer_1_funct3_out, multiplexer_6_out,
       undriven_7;
  wire [3:0] inter_stage_buffer_1_inst_encoded_s2, undriven_9;
  wire [4:0] idecoder_1_p2, idecoder_1_p3, idecoder_1_p4, op_fwd_check_1_rd_stage2;
  wire [6:0] inter_stage_buffer_1_funct7_out, multiplexer_5_out, undriven_8;
  wire [15:0] register_1_q, register_1_q_2;
  wire [15:14] alu_v1_1_alu_addr_out_2;
  wire [29:0] alu_v1_1_alu_addr_out;
  wire [31:0] adder_1_out, adder_2_out, idecoder_1_p5, idecoder_1_p6, inter_stage_buffer_1_out_11,
       inter_stage_buffer_1_out_12, inter_stage_buffer_1_out_13, inter_stage_buffer_1_out_14,
       memory_1_data_out, multiplexer_1_out, multiplexer_2_out, multiplexer_3_out, multiplexer_4_out,
       multiplexer_7_out, multiplexer_8_out, multiplexer_9_out, multiplexer_10_out, multiplexer_11_out,
       multiplexer_12_out, op_fwd_reg_q, ram_2_dout, regfile32x32_1_rs1_val, regfile32x32_1_rs2_val,
       register_2_q, register_4_q, undriven, undriven_6;
  wire [31:2] rg_pc_q;

  Register #(.width(32)) register_1 (
    .D(adder_1_out), .en(register_3_q), .clk(C), .Q({register_1_q_2, register_1_q}), .clr(rst));
  Adder #(.width(32)) adder_1 (.a({register_1_q_2, register_1_q}), .b(32'h1), .out(adder_1_out));  // open: cin, cout
  Clock clock_1 (.out(C));
  Multiplexer #(.width(32)) multiplexer_1 (
    .in0({rg_pc_q, 2'b00}), .in1(inter_stage_buffer_1_out_11), .out(multiplexer_1_out), .sel(undriven_2));
  // Probe on inter_stage_buffer_1_out_11
  // Probe on {rg_pc_q, 2'b00}
  Multiplexer #(.select(2), .width(32)) multiplexer_2 (
    .in0(32'h4), .in1(idecoder_1_p5), .in2(undriven), .in3(register_2_q), .out(multiplexer_2_out),
    .sel(undriven_3));
  RAM #(.addrWidth(16), .asyncread("true"), .dataWidth(32)) ram_1 (
    .addr(register_1_q), .we(register_3_q), .oe(1'b0), .clk(C), .din(inter_stage_buffer_1_out_11));  // open: dout
  // Probe on adder_2_out
  Multiplexer #(.width(32)) multiplexer_3 (
    .in0(multiplexer_1_out), .in1(multiplexer_4_out), .out(multiplexer_3_out), .sel(undriven_4));
  Adder #(.width(32)) adder_2 (
    .a(multiplexer_3_out), .b(multiplexer_2_out), .out(adder_2_out), .cin(1'b0));  // open: cout
  Register #(.width(30)) rg_pc (.D(adder_2_out[31:2]), .en(1'b1), .clk(C), .Q(rg_pc_q), .clr(rst));
  RAM #(.addrWidth(12), .asyncread("true"), .dataWidth(32)) ram_2 (
    .addr(rg_pc_q[13:2]), .we(1'b0), .oe(1'b1), .clk(C), .din({32{1'b0}}), .dout(ram_2_dout));
  // Probe on ram_2_dout
  // idecoder idecoder_1: pin names not known; wires that end beside it: ram_2_dout, idecoder_1_p2, idecoder_1_p3, idecoder_1_p4, idecoder_1_p5, idecoder_1_p6
  Multiplexer #(.width(32)) multiplexer_4 (
    .in0(regfile32x32_1_rs1_val), .in1(multiplexer_12_out), .out(multiplexer_4_out),
    .sel(op_fwd_check_1_rs1_s1_dep_detected));
  regfile32x32 regfile32x32_1 (
    .rd_wr_en(control_unit_ew_stage2_1_rd_in_commit), .rd_wr_val(multiplexer_12_out),
    .rd_wr_sel(op_fwd_check_1_rd_stage2), .rs1_sel(idecoder_1_p3), .rs2_sel(idecoder_1_p4), .clk(C),
    .rst(rst), .rs1_val(regfile32x32_1_rs1_val), .rs2_val(regfile32x32_1_rs2_val));
  Register #(.width(32)) register_2 (.D(idecoder_1_p6), .en(undriven_10), .clk(C), .Q(register_2_q), .clr(rst));
  Register #(.width(1)) register_3 (.D(undriven_10), .en(1'b1), .clk(C), .Q(register_3_q), .clr(rst));
  inter_stage_buffer inter_stage_buffer_1 (
    .in_5(undriven_6), .inst_encoded_s1(undriven_9), .funct3_in(undriven_7), .funct7_in(undriven_8),
    .in_4(regfile32x32_1_rs2_val), .in_2(regfile32x32_1_rs1_val), .in_1({rg_pc_q, 2'b00}), .clk(C),
    .rst(rst), .rdy_stall(undriven_10), .inst_encoded_s2(inter_stage_buffer_1_inst_encoded_s2),
    .out_13(inter_stage_buffer_1_out_13), .out_14(inter_stage_buffer_1_out_14),
    .funct3_out(inter_stage_buffer_1_funct3_out), .funct7_out(inter_stage_buffer_1_funct7_out),
    .out_11(inter_stage_buffer_1_out_11), .out_12(inter_stage_buffer_1_out_12));
  op_fwd_check op_fwd_check_1 (
    .S2_prev_rd(idecoder_1_p2), .prev_rd_in(undriven_10), .clk(C), .rst(rst), .curr_rs1(idecoder_1_p3),
    .curr_rs2(idecoder_1_p4), .rd_fwd_disable(control_unit_ew_stage2_1_rd_in_commit),
    .rs1_rs2_fwd_disable(undriven_5), .rd_stage2(op_fwd_check_1_rd_stage2),
    .rs1_s2_dep_detected(op_fwd_check_1_rs1_s2_dep_detected),
    .rs2_s2_dep_detected(op_fwd_check_1_rs2_s2_dep_detected), .rs2_store_fwd(op_fwd_check_1_rs2_store_fwd),
    .rs1_s1_dep_detected(op_fwd_check_1_rs1_s1_dep_detected));
  Multiplexer #(.width(7)) multiplexer_5 (
    .in0({7{1'b0}}), .in1(inter_stage_buffer_1_funct7_out), .out(multiplexer_5_out),
    .sel(control_unit_ew_stage2_1_funct_7));
  Multiplexer #(.width(3)) multiplexer_6 (
    .in0(inter_stage_buffer_1_funct3_out), .in1(3'b000), .out(multiplexer_6_out),
    .sel(control_unit_ew_stage2_1_s2_br_inst));
  Multiplexer #(.width(32)) multiplexer_7 (
    .in0(inter_stage_buffer_1_out_12), .in1(inter_stage_buffer_1_out_11), .out(multiplexer_7_out),
    .sel(control_unit_ew_stage2_1_opcode_a_sel_pc_or_reg));
  Multiplexer #(.width(32)) multiplexer_8 (
    .in0(inter_stage_buffer_1_out_13), .in1(inter_stage_buffer_1_out_14), .out(multiplexer_8_out),
    .sel(control_unit_ew_stage2_1_opcode_b_sel_reg_or_imm));
  control_unit_ew_stage2 control_unit_ew_stage2_1 (
    .funct3(inter_stage_buffer_1_funct3_out), .inst_type_decode(inter_stage_buffer_1_inst_encoded_s2),
    .nop_stall(register_3_q), .funct_7(control_unit_ew_stage2_1_funct_7),
    .opcode_a_sel_pc_or_reg(control_unit_ew_stage2_1_opcode_a_sel_pc_or_reg),
    .opcode_b_sel_reg_or_imm(control_unit_ew_stage2_1_opcode_b_sel_reg_or_imm),
    .mem_wr_en_cntrl(control_unit_ew_stage2_1_mem_wr_en_cntrl),
    .data_wb_or_load(control_unit_ew_stage2_1_data_wb_or_load),
    .mem_strobe(control_unit_ew_stage2_1_mem_strobe), .rd_in_commit(control_unit_ew_stage2_1_rd_in_commit),
    .funct3_sel(control_unit_ew_stage2_1_funct3_sel), .s2_br_inst(control_unit_ew_stage2_1_s2_br_inst));
  Multiplexer #(.width(32)) multiplexer_9 (
    .in0(multiplexer_7_out), .in1(op_fwd_reg_q), .out(multiplexer_9_out),
    .sel(op_fwd_check_1_rs1_s2_dep_detected));
  Multiplexer #(.width(32)) multiplexer_10 (
    .in0(multiplexer_8_out), .in1(op_fwd_reg_q), .out(multiplexer_10_out),
    .sel(op_fwd_check_1_rs2_s2_dep_detected));
  // Probe on multiplexer_11_out
  Multiplexer #(.width(32)) multiplexer_11 (
    .in0(inter_stage_buffer_1_out_13), .in1(op_fwd_reg_q), .out(multiplexer_11_out),
    .sel(op_fwd_check_1_rs2_store_fwd));
  // Probe on multiplexer_12_out
  alu_v1 alu_v1_1 (
    .a_input(multiplexer_9_out), .b_input(multiplexer_10_out), .func_3(multiplexer_6_out),
    .func_7(multiplexer_5_out[5]),
    .ALU_ADDR_OUT({alu_v1_1_alu_addr_out[29:14], alu_v1_1_alu_addr_out_2, alu_v1_1_alu_addr_out[13:0]}),
    .branch_result(alu_v1_1_branch_result));
  Multiplexer #(.width(32)) multiplexer_12 (
    .in0({alu_v1_1_alu_addr_out[29:14], alu_v1_1_alu_addr_out_2, alu_v1_1_alu_addr_out[13:0]}),
    .in1(memory_1_data_out), .out(multiplexer_12_out), .sel(control_unit_ew_stage2_1_data_wb_or_load));
  // Probe on {alu_v1_1_alu_addr_out[29:14], alu_v1_1_alu_addr_out_2, alu_v1_1_alu_addr_out[13:0]}
  Register #(.width(32)) op_fwd_reg (.D(multiplexer_12_out), .en(1'b1), .clk(C), .Q(op_fwd_reg_q), .clr(rst));
  Register #(.width(32)) register_4 (.D(multiplexer_11_out), .en(and_1_out), .clk(C), .Q(register_4_q), .clr(rst));
  and and_1 (and_1_out, alu_v1_1_alu_addr_out_2[14], alu_v1_1_alu_addr_out_2[15], control_unit_ew_stage2_1_mem_wr_en_cntrl);
  TTY #(.cols(120), .rows(48)) tty_1 (.data(multiplexer_11_out[6:0]), .clk(C), .we(and_1_out), .clr(rst));
  and and_2 (and_2_out, alu_v1_1_alu_addr_out_2[14], ~alu_v1_1_alu_addr_out_2[15]);  // AND_Gate
  // Probe on register_4_q
  memory memory_1 (
    .data_in(multiplexer_11_out), .addr(alu_v1_1_alu_addr_out[13:0]), .slave_en(and_2_out),
    .wr_en(control_unit_ew_stage2_1_mem_wr_en_cntrl), .strobe(control_unit_ew_stage2_1_mem_strobe), .clk(C),
    .data_out(memory_1_data_out));

  // Other names for the same wires on the sheet: R = rst

  // Notes on the sheet:
  //   fetch/decode unit
  //   PC + 4 -> pc 
  //   PC + imm-J -> pc 
  //   PC + imm-b -> pc -----------> depends on exc/wb -------> stall or predict then flush
  //   rs1+imm-i -> pc  -----------> depends on exc/wb -------> stall or predict then flush
  //   fix load store
  //   flushing control signal instead of data
  //   op_fwd_is trickyest please write of it
  //   Novel ideas in this arch:- 
  //   problem with branch not sending stall signal to stage2 control unit but its working because no commit in branch signal but might become problem in some case.
endmodule

module SoC (
  input  in_1,
  input  [19:0] gpio_in,
  output uart_tx,
  output [19:0] gpio_out,
  output [19:0] gpio_out_en
);

  wire C, decoder_1_out0, decoder_1_out1, decoder_1_out2, undriven;
  wire [1:0] undriven_2;
  wire [2:0] undriven_5;
  wire [3:0] undriven_9;
  wire [9:0] undriven_3;
  wire [13:12] undriven_4, undriven_6;
  wire [15:0] uart_v2_1_rd_data, undriven_7, undriven_8;
  wire [19:0] gpio_1_rd_data;
  wire [31:0] memory_1_data_out, multiplexer_1_out;

  Clock clock_1 (.out(C));
  core core_1 (.clk(undriven), .rst(undriven_7[0]));
  Decoder #(.enable("false"), .select(2)) decoder_1 (
    .out0(decoder_1_out0), .out1(decoder_1_out1), .out2(decoder_1_out2), .sel(undriven_4));  // open: out3
  memory memory_1 (
    .data_in({undriven_8, undriven_7}), .addr({undriven_6, undriven_3, undriven_2}),
    .slave_en(decoder_1_out0), .wr_en(undriven), .strobe(undriven_5), .clk(C), .data_out(memory_1_data_out));
  uart_v2 uart_v2_1 (
    .clk(C), .rst(in_1), .slave_en(decoder_1_out1), .addr(undriven_2), .write_data(undriven_7),
    .write_en(undriven), .rd_data(uart_v2_1_rd_data), .tx(uart_tx));
  gpio gpio_1 (
    .clk(C), .rst(in_1), .gpio_in(gpio_in), .slave_en(decoder_1_out2), .addr(undriven_9),
    .write_data({undriven_8[3:0], undriven_7}), .write_en(undriven), .rd_data(gpio_1_rd_data),
    .gpio_out(gpio_out), .gpio_out_en(gpio_out_en));
  Multiplexer #(.select(2), .width(32)) multiplexer_1 (
    .in0(memory_1_data_out), .in1({{16{1'b0}}, uart_v2_1_rd_data}), .in2({{12{1'b0}}, gpio_1_rd_data}),
    .in3({32{1'b0}}), .out(multiplexer_1_out), .sel(undriven_4));
  // Pins of 12 and 14 bits meet at {undriven_6, undriven_3, undriven_2}
  // Pins of 1 and 32 bits meet at {undriven_8, undriven_7}

  // Other names for the same wires on the sheet: R = in_1
endmodule

module SoC_synth (
  input  CLK,
  input  RST,
  output uart_tx,
  output [19:0] gpio_out,
  output fast_led_out
);

  wire C, core_1_p1, decoder_1_out0, decoder_1_out1, decoder_1_out2, decoder_1_out3, R,
       reset_synchronizer_0_rst_out;
  wire [1:0] core_1_p3, core_1_p3_3;
  wire [2:0] undriven;
  wire [7:0] core_1_p2_2, fast_led_1_rd_data;
  wire [11:0] core_1_p3_2;
  wire [15:0] uart_v2_1_rd_data;
  wire [19:0] gpio_1_gpio_out, gpio_1_gpio_out_en, gpio_1_rd_data;
  wire [23:0] core_1_p2;
  wire [31:0] memory_rtl_synth_1_data_out, multiplexer_1_out;

  // core core_1: pin names not known; wires that end beside it: core_1_p1, {core_1_p2_2, core_1_p2}, {core_1_p3_3, core_1_p3_2, core_1_p3}
  Decoder #(.enable("false"), .select(2)) decoder_1 (
    .out0(decoder_1_out0), .out1(decoder_1_out1), .out2(decoder_1_out2), .out3(decoder_1_out3),
    .sel(core_1_p3_3));
  reset_synchronizer reset_synchronizer_0 (.clk(CLK), .rst_in(RST), .rst_out(reset_synchronizer_0_rst_out));
  clock_divider_by2 clock_divider_by2_1 (.clk_in(CLK), .rst(reset_synchronizer_0_rst_out), .clk_out(C));
  reset_synchronizer reset_synchronizer_1 (.clk(C), .rst_in(RST), .rst_out(R));
  memory_rtl_synth memory_rtl_synth_1 (
    .data_in({core_1_p2_2, core_1_p2}), .addr({core_1_p3_2, core_1_p3}), .slave_en(decoder_1_out0),
    .wr_en(core_1_p1), .strobe(undriven), .clk(C), .data_out(memory_rtl_synth_1_data_out));
  uart_v2 uart_v2_1 (
    .clk(C), .rst(R), .slave_en(decoder_1_out1), .addr(core_1_p3), .write_data(core_1_p2[15:0]),
    .write_en(core_1_p1), .rd_data(uart_v2_1_rd_data), .tx(uart_tx));
  gpio gpio_1 (
    .clk(C), .rst(R), .gpio_in(gpio_out), .slave_en(decoder_1_out2), .addr({core_1_p3_2[1:0], core_1_p3}),
    .write_data(core_1_p2[19:0]), .write_en(core_1_p1), .rd_data(gpio_1_rd_data), .gpio_out(gpio_1_gpio_out),
    .gpio_out_en(gpio_1_gpio_out_en));
  fast_led fast_led_1 (
    .clk(C), .rst(R), .slave_en(decoder_1_out3), .addr({core_1_p3_2[0], core_1_p3}), .write_data(core_1_p2),
    .write_en(core_1_p1), .rd_data(fast_led_1_rd_data), .fast_led_out(fast_led_out));
  Multiplexer #(.select(2), .width(32)) multiplexer_1 (
    .in0(memory_rtl_synth_1_data_out), .in1({{16{1'b0}}, uart_v2_1_rd_data}),
    .in2({{12{1'b0}}, gpio_1_rd_data}), .in3({{24{1'b0}}, fast_led_1_rd_data}), .out(multiplexer_1_out),
    .sel(core_1_p3_3));
  gpio_buffer gpio_buffer_1 (.data_in(gpio_1_gpio_out), .data_en(gpio_1_gpio_out_en), .data_out(gpio_out));
endmodule

module core_v2 (
  input  clk,
  input  in_2,
  input  rst
);

  wire and_1_out, and_2_out, C, clock_1_out, comparator_1_eq, not_1_out, or_1_out, s1_s2_pipe_1_pred_out,
       s1_s2_pipe_1_s2_ready_stall, stage1_1_pred_out, stage1_1_ready_stall, stage2_1_branch,
       stage2_1_mem_wr_en, stage2_1_rd_en, stage2_1_s2_br;
  wire [1:0] stage1_1_pc;
  wire [2:0] stage2_1_strobe;
  wire [4:0] stage2_1_s2_rd_sel;
  wire [11:0] stage1_1_pc_2;
  wire [17:0] stage1_1_pc_3;
  wire [18:0] s1_s2_pipe_1_s2_inst_meta_data, stage1_1_inst_meta_data;
  wire [31:0] counter_1_q, counter_2_q, memory_1_data_out, ram_1_dout, register_1_q, s1_s2_pipe_1_s2_br_imm,
       s1_s2_pipe_1_s2_imm_val, s1_s2_pipe_1_s2_pc, s1_s2_pipe_1_s2_rs1_val, s1_s2_pipe_1_s2_rs2_val,
       stage1_1_br_imm, stage1_1_imm_stage_2, stage1_1_rs1_val, stage1_1_rs2_val, stage2_1_addr,
       stage2_1_pc_s2, stage2_1_rd_val, stage2_1_st_data;

  Clock clock_1 (.out(clock_1_out));
  assign C = or_1_out ? clock_1_out : 1'bz;  // Controlled_Buffer controlled_buffer_1
  Counter #(.max('hffffffff), .width(32)) counter_1 (
    .count(stage1_1_ready_stall), .Q(counter_1_q), .clk(C), .clr(rst));  // open: load, D, carry, up
  Counter #(.max('hffffffff), .width(32)) counter_2 (
    .Q(counter_2_q), .clk(C), .clr(rst));  // open: load, D, count, carry, up
  // Probe on counter_1_q
  or or_1 (or_1_out, not_1_out, in_2);
  // Probe on counter_2_q
  not not_1 (not_1_out, comparator_1_eq);
  Comparator #(.width(32)) comparator_1 (
    .a({stage1_1_pc_3, stage1_1_pc_2, stage1_1_pc}), .b(32'h67c), .eq(comparator_1_eq));  // open: gt, lt
  // Probe on {stage1_1_pc_3, stage1_1_pc_2, stage1_1_pc}
  // Probe on s1_s2_pipe_1_s2_pc
  RAM #(.addrWidth(12), .asyncread("true"), .dataWidth(32)) ram_1 (
    .addr(stage1_1_pc_2), .we(1'b0), .oe(1'b1), .clk(C), .din({32{1'b0}}), .dout(ram_1_dout));
  stage1 stage1_1 (
    .prev_pred_out(s1_s2_pipe_1_pred_out), .s2_br_inst(stage2_1_s2_br), .s2_rd_en(stage2_1_rd_en),
    .s2_rd_val(stage2_1_rd_val), .s2_rd_sel(stage2_1_s2_rd_sel), .branch(stage2_1_branch),
    .instruction(ram_1_dout), .s2_br_imm(s1_s2_pipe_1_s2_br_imm), .clk(C), .rst(rst),
    .prev_pc(stage2_1_pc_s2), .pc({stage1_1_pc_3, stage1_1_pc_2, stage1_1_pc}), .rs1_val(stage1_1_rs1_val),
    .rs2_val(stage1_1_rs2_val), .inst_meta_data(stage1_1_inst_meta_data), .imm_stage_2(stage1_1_imm_stage_2),
    .ready_stall(stage1_1_ready_stall), .br_imm(stage1_1_br_imm), .pred_out(stage1_1_pred_out));
  s1_s2_pipe s1_s2_pipe_1 (
    .s1_pc({stage1_1_pc_3, stage1_1_pc_2, stage1_1_pc}), .s1_rs1_val(stage1_1_rs1_val),
    .s1_rs2_val(stage1_1_rs2_val), .s1_inst_meta_data(stage1_1_inst_meta_data),
    .s1_imm_val(stage1_1_imm_stage_2), .s1_ready_stall(stage1_1_ready_stall), .s1_br_imm(stage1_1_br_imm),
    .pred(stage1_1_pred_out), .clk(C), .rst(rst), .s2_pc(s1_s2_pipe_1_s2_pc),
    .s2_rs1_val(s1_s2_pipe_1_s2_rs1_val), .s2_rs2_val(s1_s2_pipe_1_s2_rs2_val),
    .s2_inst_meta_data(s1_s2_pipe_1_s2_inst_meta_data), .s2_imm_val(s1_s2_pipe_1_s2_imm_val),
    .s2_ready_stall(s1_s2_pipe_1_s2_ready_stall), .s2_br_imm(s1_s2_pipe_1_s2_br_imm),
    .pred_out(s1_s2_pipe_1_pred_out));
  // Probe on stage2_1_st_data
  // Probe on stage2_1_st_data
  // Probe on memory_1_data_out
  // Probe on memory_1_data_out
  stage2 stage2_1 (
    .ld_data(memory_1_data_out), .s2_pc(s1_s2_pipe_1_s2_pc), .s2_rs1_val(s1_s2_pipe_1_s2_rs1_val),
    .s2_rs2_val(s1_s2_pipe_1_s2_rs2_val), .s2_inst_meta_data(s1_s2_pipe_1_s2_inst_meta_data),
    .s2_imm_val(s1_s2_pipe_1_s2_imm_val), .s2_ready_stall(s1_s2_pipe_1_s2_ready_stall),
    .s2_rd_sel(stage2_1_s2_rd_sel), .rd_en(stage2_1_rd_en), .rd_val(stage2_1_rd_val),
    .branch(stage2_1_branch), .addr(stage2_1_addr), .mem_wr_en(stage2_1_mem_wr_en), .strobe(stage2_1_strobe),
    .st_data(stage2_1_st_data), .s2_br(stage2_1_s2_br), .pc_s2(stage2_1_pc_s2));
  // Probe on stage2_1_addr
  // Probe on stage2_1_addr
  and and_1 (and_1_out, stage2_1_addr[14], ~stage2_1_addr[15]);  // AND_Gate
  memory memory_1 (
    .data_in(stage2_1_st_data), .addr(stage2_1_addr[13:0]), .slave_en(and_1_out), .wr_en(stage2_1_mem_wr_en),
    .strobe(stage2_1_strobe), .clk(C), .data_out(memory_1_data_out));
  and and_2 (and_2_out, stage2_1_addr[14], stage2_1_addr[15], stage2_1_mem_wr_en);
  TTY #(.cols(30), .rows(20)) tty_1 (.data(stage2_1_st_data[6:0]), .clk(C), .we(and_2_out), .clr(rst));
  Register #(.width(32)) register_1 (.D(stage2_1_st_data), .en(and_2_out), .clk(C), .Q(register_1_q), .clr(rst));
  // Probe on register_1_q

  // Other names for the same wires on the sheet: R = rst
endmodule

module SoC_sim_v2 (
  input  RST,
  input  [19:0] gpio_in,
  output uart_tx,
  output [19:0] gpio_out,
  output [19:0] gpio_out_en
);

  wire C, core_1_p1, decoder_1_out0, decoder_1_out1, decoder_1_out2;
  wire [1:0] core_1_p3;
  wire [2:0] undriven;
  wire [11:0] core_1_p3_2;
  wire [15:0] core_1_p2, core_1_p2_2, uart_v2_1_rd_data;
  wire [15:14] core_1_p3_3;
  wire [19:0] gpio_1_rd_data;
  wire [31:0] main_memory_data_out, multiplexer_1_out;

  Clock clock_1 (.out(C));
  // core core_1: pin names not known; wires that end beside it: core_1_p1, {core_1_p2_2, core_1_p2}, {core_1_p3_3, core_1_p3_2, core_1_p3}
  Decoder #(.enable("false"), .select(2)) decoder_1 (
    .out0(decoder_1_out0), .out1(decoder_1_out1), .out2(decoder_1_out2), .sel(core_1_p3_3));  // open: out3
  memory main_memory (
    .data_in({core_1_p2_2, core_1_p2}), .addr({core_1_p3_2, core_1_p3}), .slave_en(decoder_1_out0),
    .wr_en(core_1_p1), .strobe(undriven), .clk(C), .data_out(main_memory_data_out));
  uart_v2 uart_v2_1 (
    .clk(C), .rst(RST), .slave_en(decoder_1_out1), .addr(core_1_p3), .write_data(core_1_p2),
    .write_en(core_1_p1), .rd_data(uart_v2_1_rd_data), .tx(uart_tx));
  gpio gpio_1 (
    .clk(C), .rst(RST), .gpio_in(gpio_in), .slave_en(decoder_1_out2), .addr({core_1_p3_2[1:0], core_1_p3}),
    .write_data({core_1_p2_2[3:0], core_1_p2}), .write_en(core_1_p1), .rd_data(gpio_1_rd_data),
    .gpio_out(gpio_out), .gpio_out_en(gpio_out_en));
  Multiplexer #(.select(2), .width(32)) multiplexer_1 (
    .in0(main_memory_data_out), .in1({{16{1'b0}}, uart_v2_1_rd_data}), .in2({{12{1'b0}}, gpio_1_rd_data}),
    .in3({32{1'b0}}), .out(multiplexer_1_out), .sel(core_1_p3_3));
  // Digital_Oscilloscope #(.nState(35)) digital_oscilloscope_1: pin names not known; wires that end beside it: C, uart_tx

  // Other names for the same wires on the sheet: R = RST
endmodule

module stage1 (
  input  prev_pred_out,
  input  s2_br_inst,
  input  s2_rd_en,
  input  [31:0] s2_rd_val,
  input  [4:0] s2_rd_sel,
  input  branch,
  input  [31:0] instruction,
  input  [31:0] s2_br_imm,
  input  clk,
  input  rst,
  input  [31:0] prev_pc,
  output [31:0] pc,
  output [31:0] rs1_val,
  output [31:0] rs2_val,
  output [18:0] inst_meta_data,
  output [31:0] imm_stage_2,
  output ready_stall,
  output [31:0] br_imm,
  output pred_out
);

  wire and_1_out, and_2_out, idecoder_1_pc_sel_mux_a, idecoder_1_ready_stall, not_1_out, not_2_out,
       not_3_out, xor_1_out;
  wire [1:0] idecoder_1_pc_sel_mux_b;
  wire [4:0] idecoder_1_rs1, idecoder_1_rs2;
  wire [31:0] adder_2_out, counter_1_q, counter_2_q, counter_3_q, idecoder_1_i_type_imm,
       idecoder_1_j_type_imm, multiplexer_1_out, multiplexer_2_out, multiplexer_3_out, multiplexer_4_out,
       stall;

  Counter #(.max('hffffffff), .ongoal("continue"), .width(32)) counter_1 (
    .count(ready_stall), .Q(counter_1_q), .clk(clk), .clr(rst));  // open: load, D, carry, up
  Counter #(.max('hffffffff), .ongoal("continue"), .width(32)) counter_2 (
    .count(and_1_out), .Q(counter_2_q), .clk(clk), .clr(rst));  // open: load, D, carry, up
  Counter #(.max('hffffffff), .ongoal("continue"), .width(32)) counter_3 (
    .count(and_2_out), .Q(counter_3_q), .clk(clk), .clr(rst));  // open: load, D, carry, up
  // Probe on counter_1_q
  // Probe on counter_2_q
  // Probe on counter_3_q
  Multiplexer #(.width(32)) multiplexer_1 (.in0(s2_br_imm), .in1(32'h4), .out(multiplexer_1_out), .sel(prev_pred_out));
  xor xor_1 (xor_1_out, branch, prev_pred_out);
  Adder #(.width(32)) adder_1 (.a(multiplexer_1_out), .b(prev_pc), .out(stall));  // open: cin, cout
  and and_1 (and_1_out, s2_br_inst, xor_1_out);
  not not_1 (not_1_out, xor_1_out);
  and and_2 (and_2_out, not_1_out, s2_br_inst);
  Multiplexer #(.select(2), .width(32)) multiplexer_2 (
    .in0(32'h4), .in1(idecoder_1_j_type_imm), .in2(idecoder_1_i_type_imm), .in3(br_imm),
    .out(multiplexer_2_out), .sel(idecoder_1_pc_sel_mux_b));
  Multiplexer #(.width(32)) multiplexer_3 (
    .in0({pc[31:2], 2'b00}), .in1(rs1_val), .out(multiplexer_3_out), .sel(idecoder_1_pc_sel_mux_a));
  // Probe on adder_2_out
  Adder #(.width(32)) adder_2 (
    .a(multiplexer_3_out), .b(multiplexer_2_out), .out(adder_2_out), .cin(1'b0));  // open: cout
  Multiplexer #(.width(32)) multiplexer_4 (.in0(adder_2_out), .in1(stall), .out(multiplexer_4_out), .sel(not_2_out));
  not not_2 (not_2_out, ready_stall);
  // Probe on {pc[31:2], 2'b00}
  Register #(.width(30)) rg_pc (
    .D(multiplexer_4_out[31:2]), .en(idecoder_1_ready_stall), .clk(clk), .Q(pc[31:2]), .clr(rst));
  branch_predictor branch_predictor_1 (
    .branch_sel(s2_br_inst), .prev_pc(prev_pc[7:2]), .curr_pc(pc[7:2]), .reset(rst), .clock(clk),
    .branch_taken(branch), .pred_out(pred_out));
  idecoder idecoder_1 (
    .instruction(instruction), .branch_outcome(pred_out), .rd(inst_meta_data[8:4]),
    .funct_3(inst_meta_data[11:9]), .rs1(idecoder_1_rs1), .rs2(idecoder_1_rs2),
    .funct_7(inst_meta_data[18:12]), .imm_stage_2(imm_stage_2), .j_type_imm(idecoder_1_j_type_imm),
    .b_type_imm(br_imm), .I_type_imm(idecoder_1_i_type_imm), .ins_encoding_stage2(inst_meta_data[3:0]),
    .pc_sel_mux_a(idecoder_1_pc_sel_mux_a), .pc_sel_mux_b(idecoder_1_pc_sel_mux_b),
    .ready_stall(idecoder_1_ready_stall));
  regfile32x32 regfile32x32_1 (
    .rd_wr_en(s2_rd_en), .rd_wr_val(s2_rd_val), .rd_wr_sel(s2_rd_sel), .rs1_sel(idecoder_1_rs1),
    .rs2_sel(idecoder_1_rs2), .clk(clk), .rst(rst), .rs1_val(rs1_val), .rs2_val(rs2_val));
  not not_3 (not_3_out, and_1_out);
  and and_3 (ready_stall, idecoder_1_ready_stall, not_3_out);

  assign pc[1:0] = 2'b00;

  // Other names for the same wires on the sheet: C = clk; R = rst; ready = ready_stall; rs1_jalr[31:0] = rs1_val

  // Notes on the sheet:
  //   pc
endmodule

module s1_s2_pipe (
  input  [31:0] s1_pc,
  input  [31:0] s1_rs1_val,
  input  [31:0] s1_rs2_val,
  input  [18:0] s1_inst_meta_data,
  input  [31:0] s1_imm_val,
  input  s1_ready_stall,
  input  [31:0] s1_br_imm,
  input  pred,
  input  clk,
  input  rst,
  output [31:0] s2_pc,
  output [31:0] s2_rs1_val,
  output [31:0] s2_rs2_val,
  output [18:0] s2_inst_meta_data,
  output [31:0] s2_imm_val,
  output s2_ready_stall,
  output [31:0] s2_br_imm,
  output pred_out
);

  Register #(.width(32)) register_1 (.D(s1_pc), .en(s1_ready_stall), .clk(clk), .Q(s2_pc), .clr(rst));
  Register #(.width(32)) register_2 (.D(s1_rs1_val), .en(s1_ready_stall), .clk(clk), .Q(s2_rs1_val), .clr(rst));
  Register #(.width(32)) register_3 (.D(s1_rs2_val), .en(s1_ready_stall), .clk(clk), .Q(s2_rs2_val), .clr(rst));
  Register #(.width(19)) register_4 (
    .D(s1_inst_meta_data), .en(s1_ready_stall), .clk(clk), .Q(s2_inst_meta_data), .clr(rst));
  Register #(.width(32)) register_5 (.D(s1_imm_val), .en(s1_ready_stall), .clk(clk), .Q(s2_imm_val), .clr(rst));
  Register #(.width(1)) register_6 (.D(s1_ready_stall), .en(1'b1), .clk(clk), .Q(s2_ready_stall), .clr(rst));
  Register #(.width(32)) register_7 (.D(s1_br_imm), .en(s1_ready_stall), .clk(clk), .Q(s2_br_imm), .clr(rst));
  Register #(.width(1)) register_8 (.D(pred), .en(s1_ready_stall), .clk(clk), .Q(pred_out), .clr(rst));
endmodule

module stage2 (
  input  [31:0] ld_data,
  input  [31:0] s2_pc,
  input  [31:0] s2_rs1_val,
  input  [31:0] s2_rs2_val,
  input  [18:0] s2_inst_meta_data,
  input  [31:0] s2_imm_val,
  input  s2_ready_stall,
  output [4:0] s2_rd_sel,
  output rd_en,
  output [31:0] rd_val,
  output branch,
  output [31:0] addr,
  output mem_wr_en,
  output [2:0] strobe,
  output [31:0] st_data,
  output s2_br,
  output [31:0] pc_s2
);

  wire control_unit_ew_stage2_1_data_wb_or_load, control_unit_ew_stage2_1_funct3_sel,
       control_unit_ew_stage2_1_funct_7, control_unit_ew_stage2_1_opcode_a_sel_pc_or_reg,
       control_unit_ew_stage2_1_opcode_b_sel_reg_or_imm;

  control_unit_ew_stage2 control_unit_ew_stage2_1 (
    .funct3(s2_inst_meta_data[11:9]), .inst_type_decode(s2_inst_meta_data[3:0]), .nop_stall(s2_ready_stall),
    .funct_7(control_unit_ew_stage2_1_funct_7),
    .opcode_a_sel_pc_or_reg(control_unit_ew_stage2_1_opcode_a_sel_pc_or_reg),
    .opcode_b_sel_reg_or_imm(control_unit_ew_stage2_1_opcode_b_sel_reg_or_imm), .mem_wr_en_cntrl(mem_wr_en),
    .data_wb_or_load(control_unit_ew_stage2_1_data_wb_or_load), .mem_strobe(strobe), .rd_in_commit(rd_en),
    .funct3_sel(control_unit_ew_stage2_1_funct3_sel), .s2_br_inst(s2_br));
  alu_v3 alu_v3_1 (
    .a_input(s2_rs1_val), .pc(s2_pc), .b_input(s2_rs2_val), .imm(s2_imm_val),
    .func_7(s2_inst_meta_data[18:12]), .func_3(s2_inst_meta_data[11:9]),
    .rs1_pc_sel(control_unit_ew_stage2_1_opcode_a_sel_pc_or_reg),
    .rs2_imm_sel(control_unit_ew_stage2_1_opcode_b_sel_reg_or_imm),
    .func_7_sel(control_unit_ew_stage2_1_funct_7), .func3_sel(control_unit_ew_stage2_1_funct3_sel),
    .ALU_ADDR_OUT(addr), .branch_result(branch), .store_data(st_data));
  Multiplexer #(.width(32)) multiplexer_1 (
    .in0(addr), .in1(ld_data), .out(rd_val), .sel(control_unit_ew_stage2_1_data_wb_or_load));

  assign pc_s2 = s2_pc;
  assign s2_rd_sel = s2_inst_meta_data[8:4];
endmodule

module s2_fwd_pipe (
  input  rs1_dep,
  input  rs2_dep,
  input  non_rd_fwd_disable,
  input  [31:0] s2_exe_in,
  input  clk,
  input  rst,
  output s2_rs1_dep_out,
  output s2_rs2_dep_out,
  output [31:0] exe_out
);

  wire register_1_q, register_2_q, register_3_q;

  Register #(.width(1)) register_1 (.D(rs1_dep), .en(1'b1), .clk(clk), .Q(register_1_q), .clr(rst));
  Register #(.width(1)) register_2 (.D(rs2_dep), .en(1'b1), .clk(clk), .Q(register_2_q), .clr(rst));
  Register #(.width(1)) register_3 (.D(non_rd_fwd_disable), .en(1'b1), .clk(clk), .Q(register_3_q), .clr(rst));
  Register #(.width(32)) op_fwd_reg (.D(s2_exe_in), .en(1'b1), .clk(clk), .Q(exe_out), .clr(rst));
  and and_1 (s2_rs1_dep_out, register_1_q, register_3_q);
  and and_2 (s2_rs2_dep_out, register_2_q, register_3_q);
endmodule

// decoder
module idecoder (
  input  [31:0] instruction,
  input  branch_outcome,
  output [4:0] rd,
  output [2:0] funct_3,
  output [4:0] rs1,
  output [4:0] rs2,
  output [6:0] funct_7,
  output [31:0] imm_stage_2,
  output [31:0] j_type_imm,
  output [31:0] b_type_imm,
  output [31:0] I_type_imm,
  output [3:0] ins_encoding_stage2,
  output pc_sel_mux_a,
  output [1:0] pc_sel_mux_b,
  output ready_stall
);

  wire and_1_out, and_2_out, not_1_out, or_1_out, or_2_out, or_3_out, or_4_out, rs1_sel, rs2_sel;
  wire [1:0] imm_select;
  wire [7:0] comparator_1_eq;
  wire [11:0] bit_extender_3_out;

  assign I_type_imm[31:11] = {{20{instruction[31]}}, instruction[31]};  // Bit_Extender bit_extender_1
  assign b_type_imm[31:12] = {{19{instruction[31]}}, instruction[31]};  // Bit_Extender bit_extender_2
  Comparator #(.mode("unsigned"), .width(7)) comparator_1 (
    .a(instruction[6:0]), .b(7'b0110111), .eq(comparator_1_eq[0]));  // open: gt, lt
  Comparator #(.mode("unsigned"), .width(7)) comparator_2 (
    .a(instruction[6:0]), .b(7'b0010111), .eq(comparator_1_eq[1]));  // open: gt, lt
  Comparator #(.mode("unsigned"), .width(7)) comparator_3 (
    .a(instruction[6:0]), .b(7'b1101111), .eq(comparator_1_eq[2]));  // open: gt, lt
  Comparator #(.mode("unsigned"), .width(7)) comparator_4 (
    .a(instruction[6:0]), .b(7'b1100111), .eq(pc_sel_mux_a));  // open: gt, lt
  Comparator #(.mode("unsigned"), .width(7)) comparator_5 (
    .a(instruction[6:0]), .b(7'b1100011), .eq(comparator_1_eq[4]));  // open: gt, lt
  Comparator #(.mode("unsigned"), .width(7)) comparator_6 (
    .a(instruction[6:0]), .b(7'b0000011), .eq(comparator_1_eq[5]));  // open: gt, lt
  Comparator #(.mode("unsigned"), .width(7)) comparator_7 (
    .a(instruction[6:0]), .b(7'b0100011), .eq(comparator_1_eq[6]));  // open: gt, lt
  Comparator #(.mode("unsigned"), .width(7)) comparator_8 (
    .a(instruction[6:0]), .b(7'b0010011), .eq(comparator_1_eq[7]));  // open: gt, lt
  Comparator #(.mode("unsigned"), .width(7)) comparator_9 (
    .a(instruction[6:0]), .b(7'b0110011), .eq(ins_encoding_stage2[3]));  // open: gt, lt
  assign bit_extender_3_out = {{11{1'b0}}, 1'b0};  // Bit_Extender bit_extender_3
  assign j_type_imm[31:20] = {{11{instruction[31]}}, instruction[31]};  // Bit_Extender bit_extender_4
  Multiplexer #(.width(5)) multiplexer_1 (.in0({5{1'b0}}), .in1(instruction[24:20]), .out(rs2), .sel(rs2_sel));
  Multiplexer #(.width(5)) multiplexer_2 (.in0(instruction[19:15]), .in1({5{1'b0}}), .out(rs1), .sel(rs1_sel));
  Multiplexer #(.select(2), .width(32)) multiplexer_3 (
    .in0({instruction[31:12], bit_extender_3_out}),
    .in1({I_type_imm[31:11], instruction[30:25], instruction[11:7]}),
    .in2({I_type_imm[31:11], instruction[30:20]}), .in3(32'h4), .out(imm_stage_2), .sel(imm_select));
  not not_1 (not_1_out, branch_outcome);
  and and_1 (and_1_out, comparator_1_eq[4], branch_outcome);
  and and_2 (and_2_out, comparator_1_eq[4], not_1_out);
  or or_1 (or_1_out, and_2_out, comparator_1_eq[0], comparator_1_eq[1], comparator_1_eq[5], comparator_1_eq[6], comparator_1_eq[7], ins_encoding_stage2[3]);
  priority_encoder priority_encoder_1 (
    .input0(or_1_out), .input1(comparator_1_eq[2]), .input2(pc_sel_mux_a), .input3(and_1_out),
    .out_addr(pc_sel_mux_b));
  or or_2 (or_2_out, comparator_1_eq[2], pc_sel_mux_a);
  or or_3 (or_3_out, comparator_1_eq[0], comparator_1_eq[1]);
  or or_4 (or_4_out, comparator_1_eq[5], comparator_1_eq[7]);
  priority_encoder priority_encoder_2 (
    .input0(or_3_out), .input1(comparator_1_eq[6]), .input2(or_4_out), .input3(or_2_out),
    .out_addr(imm_select));
  or or_5 (rs1_sel, comparator_1_eq[0], comparator_1_eq[1], comparator_1_eq[2]);
  or or_6 (rs2_sel, comparator_1_eq[4], comparator_1_eq[6], ins_encoding_stage2[3]);
  or or_7 (ins_encoding_stage2[2], comparator_1_eq[4], comparator_1_eq[5], comparator_1_eq[6], comparator_1_eq[7]);
  or or_8 (ins_encoding_stage2[1], comparator_1_eq[2], pc_sel_mux_a, comparator_1_eq[6], comparator_1_eq[7]);
  or or_9 (ins_encoding_stage2[0], comparator_1_eq[1], pc_sel_mux_a, comparator_1_eq[5], comparator_1_eq[7]);
  or or_10 (ready_stall, comparator_1_eq[0], comparator_1_eq[1], comparator_1_eq[2], pc_sel_mux_a, comparator_1_eq[4], comparator_1_eq[5], comparator_1_eq[6], comparator_1_eq[7], ins_encoding_stage2[3]);

  assign b_type_imm[11:0] = {instruction[7], instruction[30:25], instruction[11:8], 1'b0};
  assign funct_3 = instruction[14:12];
  assign funct_7 = instruction[31:25];
  assign I_type_imm[10:0] = instruction[30:20];
  assign j_type_imm[19:0] = {instruction[19:12], instruction[20], instruction[30:21], 1'b0};
  assign rd = instruction[11:7];

  // Other names for the same wires on the sheet: f7[6:0] = instruction[31:25]; f7_1 = instruction[31];
  //   rd_1 = instruction[7]; rd_4[3:0] = instruction[11:8]; opcode[6:0] = instruction[6:0];
  //   rs2_4[3:0] = instruction[24:21]; rs2_t[4:0] = instruction[24:20]; f7_6[5:0] = instruction[30:25];
  //   rs2_1 = instruction[20]; f3[2:0] = instruction[14:12]; rs1_t[4:0] = instruction[19:15]

  // Notes on the sheet:
  //   0-6 (7) opcode
  //   7 (1) rd / imm
  //   8-11 (4) rd / imm
  //   12-14 (3) funct3 / imm 
  //   15 -19 (5) rs1/ imm
  //   21-24 (4) rs2 / imm
  //   31 (1) funct7 / imm
  //   20 (1) rs2 / imm
  //   25-30 (6) funct7/ imm
  //   u_type_lui
  //   u_type_auipc
  //   j_type_jal
  //   i_type_jalr
  //   b_type
  //   i_type_load
  //   s_type_store
  //   i_type
  //   r_type
  //   u_type_imm
  //   s_type_imm
  //   u_type_lui
  //   u_type_auipc
  //   j_type_jal
  //   i_type
  //   r_type
  //   i_type_jalr
  //   b_type
  //   i_type_load
  //   s_type_store
  //   why dissable the signal for store because rs2 alu port is engage/busy for immidiate rs1 + imm_i so it should not forward any thing but seperate op_fwd signal is implemented
endmodule

module branch_unit (
  input  [31:0] in_1,
  input  [31:0] in_2,
  input  [2:0] in_3,
  output branch_result
);

  wire comparator_1_eq, comparator_1_lt, comparator_2_lt, not_1_out, not_2_out, not_3_out;

  Comparator #(.width(32)) comparator_1 (.a(in_1), .b(in_2), .eq(comparator_1_eq), .lt(comparator_1_lt));  // open: gt
  Comparator #(.mode("unsigned"), .width(32)) comparator_2 (.a(in_1), .b(in_2), .lt(comparator_2_lt));  // open: gt, eq
  not not_1 (not_1_out, comparator_1_eq);
  Multiplexer #(.select(3)) multiplexer_1 (
    .in0(comparator_1_eq), .in1(not_1_out), .in2(1'b0), .in3(1'b0), .in4(comparator_1_lt), .in5(not_2_out),
    .in6(comparator_2_lt), .in7(not_3_out), .out(branch_result), .sel(in_3));
  not not_2 (not_2_out, comparator_1_lt);
  not not_3 (not_3_out, comparator_2_lt);
endmodule

module regfile32x32 (
  input  rd_wr_en,
  input  [31:0] rd_wr_val,
  input  [4:0] rd_wr_sel,
  input  [4:0] rs1_sel,
  input  [4:0] rs2_sel,
  input  clk,
  input  rst,
  output [31:0] rs1_val,
  output [31:0] rs2_val
);

  wire and_1_out, and_2_out, comparator_1_eq, comparator_2_eq, comparator_3_eq, comparator_4_eq,
       decoder_1_out0, decoder_1_out1, decoder_1_out2, decoder_1_out3, decoder_1_out4, decoder_1_out5,
       decoder_1_out6, decoder_1_out7, decoder_1_out8, decoder_1_out9, decoder_1_out10, decoder_1_out11,
       decoder_1_out12, decoder_1_out13, decoder_1_out14, decoder_1_out15, decoder_1_out16, decoder_1_out17,
       decoder_1_out18, decoder_1_out19, decoder_1_out20, decoder_1_out21, decoder_1_out22, decoder_1_out23,
       decoder_1_out24, decoder_1_out25, decoder_1_out26, decoder_1_out27, decoder_1_out28, decoder_1_out29,
       decoder_1_out30, decoder_1_out31;
  wire [31:0] multiplexer_1_out, multiplexer_2_out, multiplexer_3_out, multiplexer_4_out, register_1_q,
       register_2_q, register_3_q, register_4_q, register_5_q, register_6_q, register_7_q, register_8_q,
       register_9_q, register_10_q, register_11_q, register_12_q, register_13_q, register_14_q,
       register_15_q, register_16_q, register_17_q, register_18_q, register_19_q, register_20_q,
       register_21_q, register_22_q, register_23_q, register_24_q, register_25_q, register_26_q,
       register_27_q, register_28_q, register_29_q, register_30_q, register_31_q;

  Decoder #(.select(5)) decoder_1 (
    .out0(decoder_1_out0), .out1(decoder_1_out1), .out2(decoder_1_out2), .out3(decoder_1_out3),
    .out4(decoder_1_out4), .out5(decoder_1_out5), .out6(decoder_1_out6), .out7(decoder_1_out7),
    .out8(decoder_1_out8), .out9(decoder_1_out9), .out10(decoder_1_out10), .out11(decoder_1_out11),
    .out12(decoder_1_out12), .out13(decoder_1_out13), .out14(decoder_1_out14), .out15(decoder_1_out15),
    .out16(decoder_1_out16), .out17(decoder_1_out17), .out18(decoder_1_out18), .out19(decoder_1_out19),
    .out20(decoder_1_out20), .out21(decoder_1_out21), .out22(decoder_1_out22), .out23(decoder_1_out23),
    .out24(decoder_1_out24), .out25(decoder_1_out25), .out26(decoder_1_out26), .out27(decoder_1_out27),
    .out28(decoder_1_out28), .out29(decoder_1_out29), .out30(decoder_1_out30), .out31(decoder_1_out31),
    .sel(rd_wr_sel), .en(rd_wr_en));
  Register #(.width(32)) register_1 (.D(rd_wr_val), .en(decoder_1_out8), .clk(clk), .Q(register_1_q), .clr(rst));
  Register #(.width(32)) register_2 (.D(rd_wr_val), .en(decoder_1_out16), .clk(clk), .Q(register_2_q), .clr(rst));
  Register #(.width(32)) register_3 (.D(rd_wr_val), .en(decoder_1_out24), .clk(clk), .Q(register_3_q), .clr(rst));
  Register #(.width(32)) register_4 (.D(rd_wr_val), .en(decoder_1_out1), .clk(clk), .Q(register_4_q), .clr(rst));
  Register #(.width(32)) register_5 (.D(rd_wr_val), .en(decoder_1_out9), .clk(clk), .Q(register_5_q), .clr(rst));
  Register #(.width(32)) register_6 (.D(rd_wr_val), .en(decoder_1_out17), .clk(clk), .Q(register_6_q), .clr(rst));
  Register #(.width(32)) register_7 (.D(rd_wr_val), .en(decoder_1_out25), .clk(clk), .Q(register_7_q), .clr(rst));
  Register #(.width(32)) register_8 (.D(rd_wr_val), .en(decoder_1_out2), .clk(clk), .Q(register_8_q), .clr(rst));
  Register #(.width(32)) register_9 (.D(rd_wr_val), .en(decoder_1_out10), .clk(clk), .Q(register_9_q), .clr(rst));
  Register #(.width(32)) register_10 (.D(rd_wr_val), .en(decoder_1_out18), .clk(clk), .Q(register_10_q), .clr(rst));
  Register #(.width(32)) register_11 (.D(rd_wr_val), .en(decoder_1_out26), .clk(clk), .Q(register_11_q), .clr(rst));
  Register #(.width(32)) register_12 (.D(rd_wr_val), .en(decoder_1_out3), .clk(clk), .Q(register_12_q), .clr(rst));
  Register #(.width(32)) register_13 (.D(rd_wr_val), .en(decoder_1_out11), .clk(clk), .Q(register_13_q), .clr(rst));
  Register #(.width(32)) register_14 (.D(rd_wr_val), .en(decoder_1_out19), .clk(clk), .Q(register_14_q), .clr(rst));
  Register #(.width(32)) register_15 (.D(rd_wr_val), .en(decoder_1_out27), .clk(clk), .Q(register_15_q), .clr(rst));
  Register #(.width(32)) register_16 (.D(rd_wr_val), .en(decoder_1_out4), .clk(clk), .Q(register_16_q), .clr(rst));
  Register #(.width(32)) register_17 (.D(rd_wr_val), .en(decoder_1_out12), .clk(clk), .Q(register_17_q), .clr(rst));
  Register #(.width(32)) register_18 (.D(rd_wr_val), .en(decoder_1_out20), .clk(clk), .Q(register_18_q), .clr(rst));
  Register #(.width(32)) register_19 (.D(rd_wr_val), .en(decoder_1_out28), .clk(clk), .Q(register_19_q), .clr(rst));
  Register #(.width(32)) register_20 (.D(rd_wr_val), .en(decoder_1_out5), .clk(clk), .Q(register_20_q), .clr(rst));
  Register #(.width(32)) register_21 (.D(rd_wr_val), .en(decoder_1_out13), .clk(clk), .Q(register_21_q), .clr(rst));
  Register #(.width(32)) register_22 (.D(rd_wr_val), .en(decoder_1_out21), .clk(clk), .Q(register_22_q), .clr(rst));
  Register #(.width(32)) register_23 (.D(rd_wr_val), .en(decoder_1_out29), .clk(clk), .Q(register_23_q), .clr(rst));
  Register #(.width(32)) register_24 (.D(rd_wr_val), .en(decoder_1_out6), .clk(clk), .Q(register_24_q), .clr(rst));
  Register #(.width(32)) register_25 (.D(rd_wr_val), .en(decoder_1_out14), .clk(clk), .Q(register_25_q), .clr(rst));
  Register #(.width(32)) register_26 (.D(rd_wr_val), .en(decoder_1_out22), .clk(clk), .Q(register_26_q), .clr(rst));
  Register #(.width(32)) register_27 (.D(rd_wr_val), .en(decoder_1_out30), .clk(clk), .Q(register_27_q), .clr(rst));
  Register #(.width(32)) register_28 (.D(rd_wr_val), .en(decoder_1_out7), .clk(clk), .Q(register_28_q), .clr(rst));
  Register #(.width(32)) register_29 (.D(rd_wr_val), .en(decoder_1_out15), .clk(clk), .Q(register_29_q), .clr(rst));
  Register #(.width(32)) register_30 (.D(rd_wr_val), .en(decoder_1_out23), .clk(clk), .Q(register_30_q), .clr(rst));
  Register #(.width(32)) register_31 (.D(rd_wr_val), .en(decoder_1_out31), .clk(clk), .Q(register_31_q), .clr(rst));
  Multiplexer #(.select(5), .width(32)) multiplexer_1 (
    .in0({32{1'b0}}), .in1(register_4_q), .in2(register_8_q), .in3(register_12_q), .in4(register_16_q),
    .in5(register_20_q), .in6(register_24_q), .in7(register_28_q), .in8(register_1_q), .in9(register_5_q),
    .in10(register_9_q), .in11(register_13_q), .in12(register_17_q), .in13(register_21_q),
    .in14(register_25_q), .in15(register_29_q), .in16(register_2_q), .in17(register_6_q),
    .in18(register_10_q), .in19(register_14_q), .in20(register_18_q), .in21(register_22_q),
    .in22(register_26_q), .in23(register_30_q), .in24(register_3_q), .in25(register_7_q),
    .in26(register_11_q), .in27(register_15_q), .in28(register_19_q), .in29(register_23_q),
    .in30(register_27_q), .in31(register_31_q), .out(multiplexer_1_out), .sel(rs1_sel));
  Multiplexer #(.select(5), .width(32)) multiplexer_2 (
    .in0({32{1'b0}}), .in1(register_4_q), .in2(register_8_q), .in3(register_12_q), .in4(register_16_q),
    .in5(register_20_q), .in6(register_24_q), .in7(register_28_q), .in8(register_1_q), .in9(register_5_q),
    .in10(register_9_q), .in11(register_13_q), .in12(register_17_q), .in13(register_21_q),
    .in14(register_25_q), .in15(register_29_q), .in16(register_2_q), .in17(register_6_q),
    .in18(register_10_q), .in19(register_14_q), .in20(register_18_q), .in21(register_22_q),
    .in22(register_26_q), .in23(register_30_q), .in24(register_3_q), .in25(register_7_q),
    .in26(register_11_q), .in27(register_15_q), .in28(register_19_q), .in29(register_23_q),
    .in30(register_27_q), .in31(register_31_q), .out(multiplexer_2_out), .sel(rs2_sel));
  Comparator #(.width(5)) comparator_1 (.a({5{1'b0}}), .b(rs1_sel), .eq(comparator_1_eq));  // open: gt, lt
  Multiplexer #(.width(32)) multiplexer_3 (
    .in0(rd_wr_val), .in1({32{1'b0}}), .out(multiplexer_3_out), .sel(comparator_1_eq));
  Comparator #(.width(5)) comparator_2 (.a({5{1'b0}}), .b(rs2_sel), .eq(comparator_2_eq));  // open: gt, lt
  Multiplexer #(.width(32)) multiplexer_4 (
    .in0(rd_wr_val), .in1({32{1'b0}}), .out(multiplexer_4_out), .sel(comparator_2_eq));
  Multiplexer #(.width(32)) multiplexer_5 (
    .in0(multiplexer_1_out), .in1(multiplexer_3_out), .out(rs1_val), .sel(and_1_out));
  Multiplexer #(.width(32)) multiplexer_6 (
    .in0(multiplexer_2_out), .in1(multiplexer_4_out), .out(rs2_val), .sel(and_2_out));
  Comparator #(.width(5)) comparator_3 (.a(rd_wr_sel), .b(rs1_sel), .eq(comparator_3_eq));  // open: gt, lt
  Comparator #(.width(5)) comparator_4 (.a(rd_wr_sel), .b(rs2_sel), .eq(comparator_4_eq));  // open: gt, lt
  and and_1 (and_1_out, comparator_3_eq, rd_wr_en);
  and and_2 (and_2_out, comparator_4_eq, rd_wr_en);

  // Other names for the same wires on the sheet: rd_en = rd_wr_en; rd_sel[4:0] = rd_wr_sel; rd_val[31:0] = rd_wr_val
endmodule

// regfile16
module regfile16x32 (
  input  rd_wr_en,
  input  [31:0] rd_wr_val,
  input  [4:0] rd_wr_sel,
  input  [4:0] rs1_sel,
  input  [4:0] rs2_sel,
  input  clk,
  input  rst,
  output [31:0] rs1_val,
  output [31:0] rs2_val
);

  wire decoder_1_out0, decoder_1_out1, decoder_1_out2, decoder_1_out3, decoder_1_out4, decoder_1_out5,
       decoder_1_out6, decoder_1_out7, decoder_1_out8, decoder_1_out9, decoder_1_out10, decoder_1_out11,
       decoder_1_out12, decoder_1_out13, decoder_1_out14, decoder_1_out15;
  wire [31:0] x1_q, x2_q, x3_q, x4_q, x5_q, x6_q, x7_q, x8_q, x9_q, x10_q, x11_q, x12_q, x13_q, x14_q, x15_q;

  Decoder #(.select(4)) decoder_1 (
    .out0(decoder_1_out0), .out1(decoder_1_out1), .out2(decoder_1_out2), .out3(decoder_1_out3),
    .out4(decoder_1_out4), .out5(decoder_1_out5), .out6(decoder_1_out6), .out7(decoder_1_out7),
    .out8(decoder_1_out8), .out9(decoder_1_out9), .out10(decoder_1_out10), .out11(decoder_1_out11),
    .out12(decoder_1_out12), .out13(decoder_1_out13), .out14(decoder_1_out14), .out15(decoder_1_out15),
    .sel(rd_wr_sel[3:0]), .en(rd_wr_en));
  Register #(.width(32)) x8 (.D(rd_wr_val), .en(decoder_1_out8), .clk(clk), .Q(x8_q), .clr(rst));
  Register #(.width(32)) x1 (.D(rd_wr_val), .en(decoder_1_out1), .clk(clk), .Q(x1_q), .clr(rst));
  Register #(.width(32)) x9 (.D(rd_wr_val), .en(decoder_1_out9), .clk(clk), .Q(x9_q), .clr(rst));
  Register #(.width(32)) x2 (.D(rd_wr_val), .en(decoder_1_out2), .clk(clk), .Q(x2_q), .clr(rst));
  Register #(.width(32)) x10 (.D(rd_wr_val), .en(decoder_1_out10), .clk(clk), .Q(x10_q), .clr(rst));
  Register #(.width(32)) x3 (.D(rd_wr_val), .en(decoder_1_out3), .clk(clk), .Q(x3_q), .clr(rst));
  Register #(.width(32)) x11 (.D(rd_wr_val), .en(decoder_1_out11), .clk(clk), .Q(x11_q), .clr(rst));
  Register #(.width(32)) x4 (.D(rd_wr_val), .en(decoder_1_out4), .clk(clk), .Q(x4_q), .clr(rst));
  Register #(.width(32)) x12 (.D(rd_wr_val), .en(decoder_1_out12), .clk(clk), .Q(x12_q), .clr(rst));
  Register #(.width(32)) x5 (.D(rd_wr_val), .en(decoder_1_out5), .clk(clk), .Q(x5_q), .clr(rst));
  Register #(.width(32)) x13 (.D(rd_wr_val), .en(decoder_1_out13), .clk(clk), .Q(x13_q), .clr(rst));
  Register #(.width(32)) x6 (.D(rd_wr_val), .en(decoder_1_out6), .clk(clk), .Q(x6_q), .clr(rst));
  Register #(.width(32)) x14 (.D(rd_wr_val), .en(decoder_1_out14), .clk(clk), .Q(x14_q), .clr(rst));
  Register #(.width(32)) x7 (.D(rd_wr_val), .en(decoder_1_out7), .clk(clk), .Q(x7_q), .clr(rst));
  Register #(.width(32)) x15 (.D(rd_wr_val), .en(decoder_1_out15), .clk(clk), .Q(x15_q), .clr(rst));
  Multiplexer #(.select(4), .width(32)) multiplexer_1 (
    .in0({32{1'b0}}), .in1(x1_q), .in2(x2_q), .in3(x3_q), .in4(x4_q), .in5(x5_q), .in6(x6_q), .in7(x7_q),
    .in8(x8_q), .in9(x9_q), .in10(x10_q), .in11(x11_q), .in12(x12_q), .in13(x13_q), .in14(x14_q),
    .in15(x15_q), .out(rs1_val), .sel(rs1_sel[3:0]));
  Multiplexer #(.select(4), .width(32)) multiplexer_2 (
    .in0({32{1'b0}}), .in1(x1_q), .in2(x2_q), .in3(x3_q), .in4(x4_q), .in5(x5_q), .in6(x6_q), .in7(x7_q),
    .in8(x8_q), .in9(x9_q), .in10(x10_q), .in11(x11_q), .in12(x12_q), .in13(x13_q), .in14(x14_q),
    .in15(x15_q), .out(rs2_val), .sel(rs2_sel[3:0]));
  // Probe on x3_q
  // Probe on x3_q
endmodule

module alu_v1 (
  input  [31:0] a_input,
  input  [31:0] b_input,
  input  [2:0] func_3,
  input  func_7,
  output [31:0] ALU_ADDR_OUT,
  output branch_result
);

  wire comparator_1_eq, not_2_out, not_3_out, not_4_out;
  wire [0:0] comparator_1_lt, comparator_2_lt;
  wire [31:0] adder_1_out, and_1_out, multiplexer_1_out, multiplexer_2_out, not_1_out, or_1_out,
       shifter_1_out, shifter_2_out, shifter_3_out, xor_1_out;

  // Probe on a_input
  // Probe on a_input
  // Probe on a_input
  Multiplexer #(.width(32)) multiplexer_1 (.in0(b_input), .in1(not_1_out), .out(multiplexer_1_out), .sel(func_7));
  assign not_1_out = ~b_input;  // NOT_Gate not_1, 32 bits wide
  Adder #(.width(32)) adder_1 (.a(a_input), .b(multiplexer_1_out), .out(adder_1_out), .cin(func_7));  // open: cout
  Shifter #(.width(32)) shifter_1 (.in(a_input), .\dist (b_input[4:0]), .out(shifter_1_out));
  Comparator #(.width(32)) comparator_1 (
    .a(a_input), .b(b_input), .eq(comparator_1_eq), .lt(comparator_1_lt[0]));  // open: gt
  Comparator #(.mode("unsigned"), .width(32)) comparator_2 (
    .a(a_input), .b(b_input), .lt(comparator_2_lt[0]));  // open: gt, eq
  assign xor_1_out = b_input ^ a_input;  // XOR_Gate xor_1, 32 bits wide
  Shifter #(.shift("lr"), .width(32)) shifter_2 (.in(a_input), .\dist (b_input[4:0]), .out(shifter_2_out));
  Shifter #(.shift("ar"), .width(32)) shifter_3 (.in(a_input), .\dist (b_input[4:0]), .out(shifter_3_out));
  assign or_1_out = a_input | b_input;  // OR_Gate or_1, 32 bits wide
  assign and_1_out = a_input & b_input;  // AND_Gate and_1, 32 bits wide
  // Probe on b_input
  // Probe on b_input
  // Probe on b_input
  Multiplexer #(.width(32)) multiplexer_2 (
    .in0(shifter_2_out), .in1(shifter_3_out), .out(multiplexer_2_out), .sel(func_7));
  // Probe on adder_1_out
  // Probe on adder_1_out
  // Probe on adder_1_out
  Multiplexer #(.select(3), .width(32)) multiplexer_3 (
    .in0(adder_1_out), .in1(shifter_1_out), .in2({{31{1'b0}}, comparator_1_lt[0]}),
    .in3({{31{1'b0}}, comparator_2_lt[0]}), .in4(xor_1_out), .in5(multiplexer_2_out), .in6(or_1_out),
    .in7(and_1_out), .out(ALU_ADDR_OUT), .sel(func_3));
  not not_2 (not_2_out, comparator_1_eq);
  Multiplexer #(.select(3)) multiplexer_4 (
    .in0(comparator_1_eq), .in1(not_2_out), .in2(1'b0), .in3(1'b0), .in4(comparator_1_lt[0]),
    .in5(not_3_out), .in6(comparator_2_lt[0]), .in7(not_4_out), .out(branch_result), .sel(func_3));
  not not_3 (not_3_out, comparator_1_lt[0]);
  not not_4 (not_4_out, comparator_2_lt[0]);

  // Notes on the sheet:
  //   6). 110 --> OR
  //   7). 111 --> AND
  //   0). 000 --> ADD/SUB
  //   4). 100 --> XOR
  //   5). 101 --> SRL/SRA
  //   1). 001 --> SLL
  //   2). 010 --> SLT
  //   3). 011 --> SLTU, unsigned ADD/SUB
endmodule

module alu_v3 (
  input  [31:0] a_input,
  input  [31:0] pc,
  input  [31:0] b_input,
  input  [31:0] imm,
  input  [6:0] func_7,
  input  [2:0] func_3,
  input  rs1_pc_sel,
  input  rs2_imm_sel,
  input  func_7_sel,
  input  func3_sel,
  output [31:0] ALU_ADDR_OUT,
  output branch_result,
  output [31:0] store_data
);

  wire comparator_1_eq, func7_0, not_2_out, not_3_out, not_4_out, not_5_out, not_6_out;
  wire [0:0] comparator_1_lt, comparator_2_lt;
  wire [2:0] multiplexer_10_out;
  wire [4:0] multiplexer_2_out;
  wire [6:1] multiplexer_1_out;
  wire [26:0] multiplexer_2_out_2;
  wire [31:0] adder_1_out, and_1_out, multiplexer_3_out, multiplexer_4_out, multiplexer_5_out,
       multiplexer_6_out, multiplexer_7_out, multiplexer_8_out, multiplexer_9_out, multiplier_1_cout,
       multiplier_3_cout, multiplier_3_out, not_1_out, or_1_out, shifter_1_out, shifter_2_out, shifter_3_out,
       xor_1_out;
  wire [32:0] bit_extender_1_out, bit_extender_2_out, multiplier_2_cout, multiplier_2_out;

  Multiplexer #(.width(7)) multiplexer_1 (
    .in0({7{1'b0}}), .in1(func_7), .out({multiplexer_1_out, func7_0}), .sel(func_7_sel));
  Multiplexer #(.width(32)) multiplexer_2 (
    .in0(b_input), .in1(imm), .out({multiplexer_2_out_2, multiplexer_2_out}), .sel(rs2_imm_sel));
  Multiplexer #(.width(32)) multiplexer_3 (.in0(a_input), .in1(pc), .out(multiplexer_3_out), .sel(rs1_pc_sel));
  // Probe on multiplexer_3_out
  // Probe on multiplexer_3_out
  // Probe on multiplexer_3_out
  Multiplexer #(.width(32)) multiplexer_4 (
    .in0({multiplexer_2_out_2, multiplexer_2_out}), .in1(not_1_out), .out(multiplexer_4_out),
    .sel(multiplexer_1_out[5]));
  assign not_1_out = ~{multiplexer_2_out_2, multiplexer_2_out};  // NOT_Gate not_1, 32 bits wide
  Adder #(.width(32)) adder_1 (
    .a(multiplexer_3_out), .b(multiplexer_4_out), .out(adder_1_out), .cin(multiplexer_1_out[5]));  // open: cout
  Shifter #(.width(32)) shifter_1 (.in(multiplexer_3_out), .\dist (multiplexer_2_out), .out(shifter_1_out));
  Comparator #(.width(32)) comparator_1 (
    .a(multiplexer_3_out), .b({multiplexer_2_out_2, multiplexer_2_out}), .eq(comparator_1_eq),
    .lt(comparator_1_lt[0]));  // open: gt
  Comparator #(.mode("unsigned"), .width(32)) comparator_2 (
    .a(multiplexer_3_out), .b({multiplexer_2_out_2, multiplexer_2_out}), .lt(comparator_2_lt[0]));  // open: gt, eq
  assign xor_1_out = {multiplexer_2_out_2, multiplexer_2_out} ^ multiplexer_3_out;  // XOR_Gate xor_1, 32 bits wide
  Shifter #(.shift("lr"), .width(32)) shifter_2 (
    .in(multiplexer_3_out), .\dist (multiplexer_2_out), .out(shifter_2_out));
  Shifter #(.shift("ar"), .width(32)) shifter_3 (
    .in(multiplexer_3_out), .\dist (multiplexer_2_out), .out(shifter_3_out));
  assign or_1_out = multiplexer_3_out | {multiplexer_2_out_2, multiplexer_2_out};  // OR_Gate or_1, 32 bits wide
  assign and_1_out = multiplexer_3_out & {multiplexer_2_out_2, multiplexer_2_out};  // AND_Gate and_1, 32 bits wide
  // Probe on {multiplexer_2_out_2, multiplexer_2_out}
  // Probe on {multiplexer_2_out_2, multiplexer_2_out}
  // Probe on {multiplexer_2_out_2, multiplexer_2_out}
  Multiplier #(.width(32)) multiplier_1 (
    .a(multiplexer_3_out), .b({multiplexer_2_out_2, multiplexer_2_out}), .cout(multiplier_1_cout));  // open: out, cin
  Multiplexer #(.width(32)) multiplexer_5 (
    .in0(shifter_2_out), .in1(shifter_3_out), .out(multiplexer_5_out), .sel(multiplexer_1_out[5]));
  assign bit_extender_1_out = {{1{multiplexer_3_out[31]}}, multiplexer_3_out};  // Bit_Extender bit_extender_1
  assign bit_extender_2_out = {{1{1'b0}}, {multiplexer_2_out_2, multiplexer_2_out}};  // Bit_Extender bit_extender_2
  // Probe on adder_1_out
  // Probe on adder_1_out
  // Probe on adder_1_out
  Multiplier #(.mode("twosComplement"), .width(33)) multiplier_2 (
    .a(bit_extender_1_out), .b(bit_extender_2_out), .out(multiplier_2_out), .cout(multiplier_2_cout));  // open: cin
  Multiplier #(.mode("twosComplement"), .width(32)) multiplier_3 (
    .a(multiplexer_3_out), .b({multiplexer_2_out_2, multiplexer_2_out}), .out(multiplier_3_out),
    .cout(multiplier_3_cout));  // open: cin
  Multiplexer #(.width(32)) multiplexer_6 (
    .in0(multiplier_1_cout), .in1({{31{1'b0}}, comparator_2_lt[0]}), .out(multiplexer_6_out), .sel(not_2_out));
  not not_2 (not_2_out, func7_0);
  Multiplexer #(.width(32)) multiplexer_7 (
    .in0(adder_1_out), .in1(multiplier_3_out), .out(multiplexer_7_out), .sel(func7_0));
  Multiplexer #(.width(32)) multiplexer_8 (
    .in0(shifter_1_out), .in1(multiplier_3_cout), .out(multiplexer_8_out), .sel(func7_0));
  not not_3 (not_3_out, func7_0);
  Multiplexer #(.width(32)) multiplexer_9 (
    .in0({multiplier_2_cout[30:0], multiplier_2_out[32]}), .in1({{31{1'b0}}, comparator_1_lt[0]}),
    .out(multiplexer_9_out), .sel(not_3_out));
  Multiplexer #(.width(3)) multiplexer_10 (.in0(func_3), .in1(3'b000), .out(multiplexer_10_out), .sel(func3_sel));
  not not_4 (not_4_out, comparator_1_eq);
  not not_5 (not_5_out, comparator_1_lt[0]);
  not not_6 (not_6_out, comparator_2_lt[0]);
  Multiplexer #(.select(3), .width(32)) multiplexer_11 (
    .in0(multiplexer_7_out), .in1(multiplexer_8_out), .in2(multiplexer_9_out), .in3(multiplexer_6_out),
    .in4(xor_1_out), .in5(multiplexer_5_out), .in6(or_1_out), .in7(and_1_out), .out(ALU_ADDR_OUT),
    .sel(multiplexer_10_out));
  Multiplexer #(.select(3)) multiplexer_12 (
    .in0(comparator_1_eq), .in1(not_4_out), .in2(1'b0), .in3(1'b0), .in4(comparator_1_lt[0]),
    .in5(not_5_out), .in6(comparator_2_lt[0]), .in7(not_6_out), .out(branch_result), .sel(multiplexer_10_out));

  assign store_data = b_input;

  // Notes on the sheet:
  //   0). 000 --> ADD/SUB
  //   4). 100 --> XOR
  //   5). 101 --> SRL/SRA
  //   6). 110 --> OR
  //   7). 111 --> AND
  //   1). 001 --> SLL
  //   2). 010 --> SLT
  //   3). 011 --> SLTU, unsigned ADD/SUB
endmodule

module control_unit_fD_stage1 (
  input  [8:0] inst_type_decode,
  input  prev_branch_dect,
  input  branch,
  output [3:0] ins_encoding_stage2,
  output pc_sel_mux_a,
  output [1:0] pc_sel_mux_b,
  output rs1_sel,
  output rs2_sel,
  output [1:0] imm_select,
  output ready_stall,
  output pc_next_stage_sel,
  output [1:0] rs1_rs2_fwd_disable
);

  wire and_2_out, and_4_out, not_1_out, not_2_out, not_3_out, not_4_out, or_1_out, or_2_out, or_3_out,
       or_4_out, or_11_out;

  and and_1 (pc_next_stage_sel, prev_branch_dect, branch);
  not not_1 (not_1_out, pc_next_stage_sel);
  not not_2 (not_2_out, pc_next_stage_sel);
  and and_2 (and_2_out, inst_type_decode[2], not_1_out);
  and and_3 (pc_sel_mux_a, inst_type_decode[3], not_2_out);
  or or_1 (or_1_out, and_4_out, inst_type_decode[0], inst_type_decode[1], inst_type_decode[5], inst_type_decode[6], inst_type_decode[7], inst_type_decode[8]);
  not not_3 (not_3_out, branch);
  and and_4 (and_4_out, not_3_out, prev_branch_dect);
  priority_encoder priority_encoder_1 (
    .input0(or_1_out), .input1(and_2_out), .input2(pc_sel_mux_a), .input3(pc_next_stage_sel),
    .out_addr(pc_sel_mux_b));
  or or_2 (or_2_out, and_2_out, pc_sel_mux_a);
  or or_3 (or_3_out, inst_type_decode[0], inst_type_decode[1]);
  or or_4 (or_4_out, inst_type_decode[5], inst_type_decode[7]);
  priority_encoder priority_encoder_2 (
    .input0(or_3_out), .input1(inst_type_decode[6]), .input2(or_4_out), .input3(or_2_out),
    .out_addr(imm_select));
  or or_5 (rs1_sel, inst_type_decode[0], inst_type_decode[1], and_2_out);
  or or_6 (rs2_sel, inst_type_decode[4], inst_type_decode[6], inst_type_decode[8]);
  or or_7 (ins_encoding_stage2[2], inst_type_decode[4], inst_type_decode[5], inst_type_decode[6], inst_type_decode[7]);
  or or_8 (ins_encoding_stage2[1], and_2_out, pc_sel_mux_a, inst_type_decode[6], inst_type_decode[7]);
  or or_9 (ins_encoding_stage2[0], inst_type_decode[1], pc_sel_mux_a, inst_type_decode[5], inst_type_decode[7]);
  or or_10 (rs1_rs2_fwd_disable[0], pc_sel_mux_a, rs1_sel);
  or or_11 (or_11_out, inst_type_decode[0], inst_type_decode[1], and_2_out, pc_sel_mux_a, inst_type_decode[4], inst_type_decode[5], inst_type_decode[6], inst_type_decode[7], inst_type_decode[8]);
  not not_4 (not_4_out, pc_next_stage_sel);
  or or_12 (rs1_rs2_fwd_disable[1], rs1_rs2_fwd_disable[0], inst_type_decode[6]);
  and and_5 (ready_stall, or_11_out, not_4_out);

  assign ins_encoding_stage2[3] = inst_type_decode[8];

  // Notes on the sheet:
  //   u_type_lui
  //   u_type_auipc
  //   j_type_jal
  //   i_type
  //   r_type
  //   i_type_jalr
  //   b_type
  //   i_type_load
  //   s_type_store
  //   why dissable the signal for store because rs2 alu port is engage/busy for immidiate rs1 + imm_i so it should not forward any thing but seperate op_fwd signal is implemented
endmodule

module control_unit_ew_stage2 (
  input  [2:0] funct3,
  input  [3:0] inst_type_decode,
  input  nop_stall,
  output funct_7,
  output opcode_a_sel_pc_or_reg,
  output opcode_b_sel_reg_or_imm,
  output mem_wr_en_cntrl,
  output data_wb_or_load,
  output [2:0] mem_strobe,
  output rd_in_commit,
  output funct3_sel,
  output s2_br_inst
);

  wire and_1_out, and_2_out, and_3_out, not_1_out, or_5_out;
  wire [7:0] decoder_1_out0;

  Decoder #(.select(3)) decoder_1 (
    .out0(decoder_1_out0[0]), .out1(decoder_1_out0[1]), .out2(decoder_1_out0[2]), .out3(decoder_1_out0[3]),
    .out4(s2_br_inst), .out5(data_wb_or_load), .out6(mem_wr_en_cntrl), .out7(decoder_1_out0[7]),
    .sel(inst_type_decode[2:0]), .en(and_1_out));
  and and_1 (and_1_out, nop_stall, not_1_out);
  not not_1 (not_1_out, inst_type_decode[3]);
  or or_1 (opcode_a_sel_pc_or_reg, decoder_1_out0[1], decoder_1_out0[2], decoder_1_out0[3]);
  or or_2 (rd_in_commit, decoder_1_out0[0], decoder_1_out0[1], decoder_1_out0[2], decoder_1_out0[3], data_wb_or_load, decoder_1_out0[7], inst_type_decode[3]);
  or or_3 (funct3_sel, data_wb_or_load, decoder_1_out0[0], decoder_1_out0[1], decoder_1_out0[2], mem_wr_en_cntrl);
  or or_4 (opcode_b_sel_reg_or_imm, decoder_1_out0[0], decoder_1_out0[1], decoder_1_out0[2], mem_wr_en_cntrl, decoder_1_out0[3], data_wb_or_load, decoder_1_out0[7]);
  or or_5 (or_5_out, inst_type_decode[3], decoder_1_out0[7]);
  and and_2 (and_2_out, funct3[2], ~funct3[1], funct3[0]);  // AND_Gate
  and and_3 (and_3_out, or_5_out, and_2_out);
  or or_6 (funct_7, and_3_out, inst_type_decode[3]);

  assign mem_strobe = funct3;

  // Notes on the sheet:
  //   u_type_lui
  //   u_type_auipc
  //   j_type_jal
  //   b_type
  //   i_type_load
  //   i_type
  //   r_type
  //   i_type_jalr
  //   s_type_store
endmodule

module priority_encoder (
  input  input0,
  input  input1,
  input  input2,
  input  input3,
  output [1:0] out_addr
);

  wire and_1_out, not_1_out;

  not not_1 (not_1_out, input2);
  or or_1 (out_addr[1], input3, input2);
  and and_1 (and_1_out, not_1_out, input1);
  or or_2 (out_addr[0], input3, and_1_out);
endmodule

module uart_v2 (
  input  clk,
  input  rst,
  input  slave_en,
  input  [1:0] addr,
  input  [15:0] write_data,
  input  write_en,
  output [15:0] rd_data,
  output tx
);

  wire and_1_out, and_2_out, and_3_out, and_4_out, and_5_out, and_6_out, and_7_out, and_8_out, and_9_out,
       and_10_out, comparator_1_eq, decoder_1_out0, decoder_1_out2, multiplexer_3_out, multiplexer_5_out,
       nor_1_out, not_1_out, or_1_out, or_2_out, or_3_out, or_4_out, register_1_q, register_2_q, xor_1_out;
  wire [0:0] write_busy_q;
  wire [3:0] adder_2_out, multiplexer_4_out, tx_state_reg_q;
  wire [7:0] multiplexer_2_out, tx_data_reg_q;
  wire [15:0] baud_reg_q;
  wire [19:0] adder_1_out, baud_counter_q, multiplexer_1_out;

  and and_1 (and_1_out, slave_en, write_en);
  Decoder #(.enable("false"), .select(2)) decoder_1 (
    .out0(decoder_1_out0), .out2(decoder_1_out2), .sel(addr));  // open: out1, out3
  and and_2 (and_2_out, decoder_1_out2, and_1_out);
  Register #(.width(1)) write_busy (.D(and_3_out), .en(or_1_out), .clk(clk), .Q(write_busy_q[0]), .clr(rst));
  and and_3 (and_3_out, and_2_out, ~and_10_out);  // AND_Gate
  or or_1 (or_1_out, and_2_out, and_10_out);
  Adder #(.width(20)) adder_1 (.a(baud_counter_q), .b(20'h1), .out(adder_1_out), .cin(1'b0));  // open: cout
  and and_4 (and_4_out, decoder_1_out0, and_1_out);
  Multiplexer #(.width(20)) multiplexer_1 (
    .in0(adder_1_out), .in1({20{1'b0}}), .out(multiplexer_1_out), .sel(or_2_out));
  or or_2 (or_2_out, and_10_out, comparator_1_eq);
  Multiplexer #(.width(8)) multiplexer_2 (
    .in0({1'b0, tx_data_reg_q[7:1]}), .in1(write_data[7:0]), .out(multiplexer_2_out), .sel(and_2_out));
  Register #(.width(20)) baud_counter (.D(multiplexer_1_out), .en(or_3_out), .clk(clk), .Q(baud_counter_q), .clr(rst));
  or or_3 (or_3_out, write_busy_q[0], and_10_out, comparator_1_eq);
  Register #(.width(16)) baud_reg (.D(write_data), .en(and_4_out), .clk(clk), .Q(baud_reg_q), .clr(rst));
  and and_5 (and_5_out, xor_1_out, ~and_8_out);  // AND_Gate
  and and_6 (and_6_out, xor_1_out, write_busy_q[0]);
  Multiplexer multiplexer_3 (.in0(and_5_out), .in1(and_2_out), .out(multiplexer_3_out), .sel(and_7_out));
  or or_4 (or_4_out, and_6_out, and_10_out);
  Register tx_data_reg (.D(multiplexer_2_out), .en(multiplexer_3_out), .clk(clk), .Q(tx_data_reg_q), .clr(rst));
  Adder #(.width(4)) adder_2 (.a(tx_state_reg_q), .b(4'b0001), .out(adder_2_out), .cin(1'b0));  // open: cout
  Multiplexer #(.width(4)) multiplexer_4 (.in0(adder_2_out), .in1(4'b0000), .out(multiplexer_4_out), .sel(and_10_out));
  Comparator #(.mode("unsigned"), .width(20)) comparator_1 (
    .a(baud_counter_q), .b({baud_reg_q, 4'b0000}), .eq(comparator_1_eq));  // open: gt, lt
  Register #(.width(4)) tx_state_reg (.D(multiplexer_4_out), .en(or_4_out), .clk(clk), .Q(tx_state_reg_q), .clr(rst));
  Register #(.width(1)) register_1 (.D(not_1_out), .en(comparator_1_eq), .clk(clk), .Q(register_1_q), .clr(rst));
  Multiplexer multiplexer_5 (.in0(1'b1), .in1(1'b0), .out(multiplexer_5_out), .sel(and_8_out));
  Multiplexer multiplexer_6 (.in0(multiplexer_5_out), .in1(tx_data_reg_q[0]), .out(tx), .sel(nor_1_out));
  not not_1 (not_1_out, register_1_q);
  Register #(.width(1)) register_2 (.D(not_1_out), .en(write_busy_q[0]), .clk(clk), .Q(register_2_q), .clr(rst));
  nor nor_1 (nor_1_out, and_7_out, and_8_out, and_9_out, and_10_out);
  and and_7 (and_7_out, ~tx_state_reg_q[0], ~tx_state_reg_q[1], ~tx_state_reg_q[2], ~tx_state_reg_q[3]);  // AND_Gate
  and and_8 (and_8_out, tx_state_reg_q[0], ~tx_state_reg_q[1], ~tx_state_reg_q[2], ~tx_state_reg_q[3]);  // AND_Gate
  and and_9 (and_9_out, ~tx_state_reg_q[0], tx_state_reg_q[1], ~tx_state_reg_q[2], tx_state_reg_q[3]);  // AND_Gate
  and and_10 (and_10_out, tx_state_reg_q[0], tx_state_reg_q[1], ~tx_state_reg_q[2], tx_state_reg_q[3]);  // AND_Gate
  xor xor_1 (xor_1_out, not_1_out, register_2_q);
  Multiplexer #(.select(2), .width(16)) multiplexer_7 (
    .in0(baud_reg_q), .in1({16{1'b0}}), .in2({16{1'b0}}), .in3({{15{1'b0}}, write_busy_q[0]}), .out(rd_data),
    .sel(addr));

  // Other names for the same wires on the sheet: c = clk; r = rst
endmodule

module uart_v1 (
  input  clk,
  input  rst,
  input  [1:0] addr,
  input  [15:0] data_in,
  input  write_en,
  output tx
);

  wire and_1_out, and_2_out, and_3_out, and_4_out, and_5_out, and_6_out, and_7_out, comparator_1_eq,
       decoder_1_out0, decoder_1_out2, multiplexer_1_out, multiplexer_4_out, multiplexer_6_out, nor_1_out,
       not_1_out, or_1_out, or_2_out, or_3_out, or_4_out, register_1_q, register_3_q, register_4_q, xor_1_out;
  wire [3:0] adder_2_out, multiplexer_5_out, tx_state_reg_q;
  wire [7:0] multiplexer_3_out, register_2_q;
  wire [15:0] baud_reg_q;
  wire [19:0] adder_1_out, baud_counter_q, multiplexer_2_out;

  Decoder #(.enable("false"), .select(2)) decoder_1 (
    .out0(decoder_1_out0), .out2(decoder_1_out2), .sel(addr));  // open: out1, out3
  and and_1 (and_1_out, decoder_1_out2, write_en);
  Register #(.width(1)) register_1 (.D(multiplexer_1_out), .en(or_1_out), .clk(clk), .Q(register_1_q), .clr(rst));
  Multiplexer multiplexer_1 (.in0(and_1_out), .in1(1'b0), .out(multiplexer_1_out), .sel(and_7_out));
  or or_1 (or_1_out, and_1_out, and_7_out);
  Adder #(.width(20)) adder_1 (.a(baud_counter_q), .b(20'h1), .out(adder_1_out), .cin(1'b0));  // open: cout
  and and_2 (and_2_out, decoder_1_out0, write_en);
  Multiplexer #(.width(20)) multiplexer_2 (
    .in0(adder_1_out), .in1({20{1'b0}}), .out(multiplexer_2_out), .sel(or_2_out));
  or or_2 (or_2_out, and_7_out, comparator_1_eq);
  Multiplexer #(.width(8)) multiplexer_3 (
    .in0({1'b0, register_2_q[7:1]}), .in1(data_in[7:0]), .out(multiplexer_3_out), .sel(and_1_out));
  Register #(.width(20)) baud_counter (.D(multiplexer_2_out), .en(or_3_out), .clk(clk), .Q(baud_counter_q), .clr(rst));
  or or_3 (or_3_out, register_1_q, and_7_out, comparator_1_eq);
  Register #(.width(16)) baud_reg (.D(data_in), .en(and_2_out), .clk(clk), .Q(baud_reg_q), .clr(rst));
  and and_3 (and_3_out, xor_1_out, register_1_q);
  Multiplexer multiplexer_4 (.in0(xor_1_out), .in1(and_1_out), .out(multiplexer_4_out), .sel(and_4_out));
  or or_4 (or_4_out, and_3_out, and_7_out);
  Register register_2 (.D(multiplexer_3_out), .en(multiplexer_4_out), .clk(clk), .Q(register_2_q), .clr(rst));
  Adder #(.width(4)) adder_2 (.a(tx_state_reg_q), .b(4'b0001), .out(adder_2_out), .cin(1'b0));  // open: cout
  Multiplexer #(.width(4)) multiplexer_5 (.in0(adder_2_out), .in1(4'b0000), .out(multiplexer_5_out), .sel(and_7_out));
  Comparator #(.mode("unsigned"), .width(20)) comparator_1 (
    .a(baud_counter_q), .b({baud_reg_q, 4'b0000}), .eq(comparator_1_eq));  // open: gt, lt
  Register #(.width(4)) tx_state_reg (.D(multiplexer_5_out), .en(or_4_out), .clk(clk), .Q(tx_state_reg_q), .clr(rst));
  Register #(.width(1)) register_3 (.D(not_1_out), .en(comparator_1_eq), .clk(clk), .Q(register_3_q), .clr(rst));
  Multiplexer multiplexer_6 (.in0(1'b1), .in1(1'b0), .out(multiplexer_6_out), .sel(and_5_out));
  Multiplexer multiplexer_7 (.in0(multiplexer_6_out), .in1(register_2_q[0]), .out(tx), .sel(nor_1_out));
  not not_1 (not_1_out, register_3_q);
  Register #(.width(1)) register_4 (.D(not_1_out), .en(register_1_q), .clk(clk), .Q(register_4_q), .clr(rst));
  nor nor_1 (nor_1_out, and_4_out, and_5_out, and_6_out, and_7_out);
  and and_4 (and_4_out, ~tx_state_reg_q[0], ~tx_state_reg_q[1], ~tx_state_reg_q[2], ~tx_state_reg_q[3]);  // AND_Gate
  and and_5 (and_5_out, tx_state_reg_q[0], ~tx_state_reg_q[1], ~tx_state_reg_q[2], ~tx_state_reg_q[3]);  // AND_Gate
  and and_6 (and_6_out, ~tx_state_reg_q[0], tx_state_reg_q[1], ~tx_state_reg_q[2], tx_state_reg_q[3]);  // AND_Gate
  and and_7 (and_7_out, tx_state_reg_q[0], tx_state_reg_q[1], ~tx_state_reg_q[2], tx_state_reg_q[3]);  // AND_Gate
  xor xor_1 (xor_1_out, not_1_out, register_4_q);
endmodule

module gpio (
  input  clk,
  input  rst,
  input  [19:0] gpio_in,
  input  slave_en,
  input  [3:0] addr,
  input  [19:0] write_data,
  input  write_en,
  output [19:0] rd_data,
  output [19:0] gpio_out,
  output [19:0] gpio_out_en
);

  wire and_1_out, and_2_out, and_3_out, and_4_out, and_5_out, and_6_out, comparator_1_eq, register_1_q;
  wire [0:0] not_1_out;
  wire [19:0] reg_data_in_q;
  wire [31:0] adder_1_out, counter_q, multiplexer_1_out;

  and and_1 (and_1_out, ~addr[0], ~addr[1], ~addr[2], ~addr[3]);  // AND_Gate
  and and_2 (and_2_out, ~addr[0], ~addr[1], addr[2], ~addr[3]);  // AND_Gate
  and and_3 (and_3_out, slave_en, write_en);
  and and_4 (and_4_out, slave_en, write_en);
  Adder #(.width(32)) adder_1 (.a(counter_q), .b(32'h1), .out(adder_1_out), .cin(1'b0));  // open: cout
  and and_5 (and_5_out, and_4_out, and_1_out);
  and and_6 (and_6_out, and_3_out, and_2_out);
  Multiplexer #(.width(32)) multiplexer_1 (
    .in0(adder_1_out), .in1({32{1'b0}}), .out(multiplexer_1_out), .sel(comparator_1_eq));
  Register #(.width(32)) counter (.D(multiplexer_1_out), .en(1'b1), .clk(clk), .Q(counter_q), .clr(rst));
  Register #(.width(20)) reg_direction (.D(write_data), .en(and_5_out), .clk(clk), .Q(gpio_out_en), .clr(rst));
  Register #(.width(20)) reg_data_out (.D(write_data), .en(and_6_out), .clk(clk), .Q(gpio_out), .clr(rst));
  Register #(.width(20)) reg_data_in (.D(gpio_in), .en(1'b1), .clk(clk), .Q(reg_data_in_q), .clr(rst));
  Comparator #(.mode("unsigned"), .width(32)) comparator_1 (
    .a(counter_q), .b(32'h17d7840), .eq(comparator_1_eq));  // open: gt, lt
  Register #(.width(1)) register_1 (.D(not_1_out[0]), .en(comparator_1_eq), .clk(clk), .Q(register_1_q), .clr(rst));
  not not_1 (not_1_out[0], register_1_q);
  Multiplexer #(.select(2), .width(20)) multiplexer_2 (
    .in0({20{1'b0}}), .in1(reg_data_in_q), .in2({{19{1'b0}}, not_1_out[0]}), .in3({20{1'b0}}), .out(rd_data),
    .sel(addr[3:2]));

  // Other names for the same wires on the sheet: c = clk; r = rst
endmodule

module fast_led (
  input  clk,
  input  rst,
  input  slave_en,
  input  [2:0] addr,
  input  [23:0] write_data,
  input  write_en,
  output [7:0] rd_data,
  output fast_led_out
);

  wire and_1_out, and_2_out, and_3_out, and_4_out, and_5_out, and_6_out, and_7_out, and_8_out, and_9_out,
       and_10_out, comparator_1_eq, multiplexer_2_out, not_1_out, not_2_out, not_3_out, or_1_out, or_2_out,
       or_3_out, or_4_out, or_5_out, or_6_out, or_7_out;
  wire [1:0] write_busy_q;
  wire [4:0] adder_1_out, adder_2_out, multiplexer_3_out, multiplexer_4_out, multiplexer_5_out,
       multiplexer_6_out, seq_count_q, state_reg_q;
  wire [23:0] multiplexer_1_out, outstanding_req_data_q;
  wire [23:1] tx_data_reg_q;
  wire [23:23] tx_data_reg_q_2;

  not not_1 (not_1_out, addr[2]);
  and and_1 (and_1_out, slave_en, write_en);
  and and_2 (and_2_out, not_1_out, and_1_out);
  or or_1 (or_1_out, and_2_out, not_2_out);
  not not_2 (not_2_out, write_busy_q[0]);
  Register #(.width(24)) outstanding_req_data (
    .D(write_data), .en(and_2_out), .clk(clk), .Q(outstanding_req_data_q), .clr(rst));
  Register #(.width(1)) outstanding_en_status (.D(or_2_out), .en(or_1_out), .clk(clk), .Q(write_busy_q[1]), .clr(rst));
  or or_2 (or_2_out, and_2_out, write_busy_q[0]);
  and and_3 (and_3_out, write_busy_q[1], ~write_busy_q[0]);  // AND_Gate
  or or_3 (or_3_out, and_3_out, and_7_out);
  Register #(.width(1)) write_busy (.D(and_4_out), .en(or_3_out), .clk(clk), .Q(write_busy_q[0]), .clr(rst));
  and and_4 (and_4_out, and_3_out, ~and_7_out);  // AND_Gate
  Multiplexer #(.width(24)) multiplexer_1 (
    .in0({tx_data_reg_q, 1'b0}), .in1(outstanding_req_data_q), .out(multiplexer_1_out), .sel(and_3_out));
  Multiplexer multiplexer_2 (.in0(and_8_out), .in1(and_3_out), .out(multiplexer_2_out), .sel(and_6_out));
  Adder #(.width(5)) adder_1 (.a(state_reg_q), .b(5'b00001), .out(adder_1_out), .cin(1'b0));  // open: cout
  Register #(.width(24)) tx_data_reg (
    .D(multiplexer_1_out), .en(multiplexer_2_out), .clk(clk), .Q({tx_data_reg_q_2[23], tx_data_reg_q}),
    .clr(rst));
  Multiplexer #(.width(5)) multiplexer_3 (.in0(adder_1_out), .in1({5{1'b0}}), .out(multiplexer_3_out), .sel(and_7_out));
  and and_5 (and_5_out, write_busy_q[0], and_8_out);
  or or_4 (or_4_out, and_5_out, and_7_out);
  Register #(.width(5)) state_reg (.D(multiplexer_3_out), .en(or_4_out), .clk(clk), .Q(state_reg_q), .clr(rst));
  Adder #(.width(5)) adder_2 (.a(seq_count_q), .b(5'b00001), .out(adder_2_out), .cin(1'b0));  // open: cout
  Multiplexer #(.width(5)) multiplexer_4 (.in0(adder_2_out), .in1({5{1'b0}}), .out(multiplexer_4_out), .sel(or_5_out));
  or or_5 (or_5_out, and_8_out, and_7_out);
  and and_6 (and_6_out, ~state_reg_q[0], ~state_reg_q[1], ~state_reg_q[2], ~state_reg_q[3], ~state_reg_q[4]);  // AND_Gate
  and and_7 (and_7_out, ~state_reg_q[0], ~state_reg_q[1], ~state_reg_q[2], state_reg_q[3], state_reg_q[4]);  // AND_Gate
  Register #(.width(5)) seq_count (.D(multiplexer_4_out), .en(or_6_out), .clk(clk), .Q(seq_count_q), .clr(rst));
  or or_6 (or_6_out, and_7_out, write_busy_q[0]);
  Multiplexer #(.width(5)) multiplexer_5 (
    .in0({5{1'b0}}), .in1(multiplexer_6_out), .out(multiplexer_5_out), .sel(fast_led_out));
  Multiplexer #(.width(5)) multiplexer_6 (
    .in0(5'b01010), .in1(5'b10100), .out(multiplexer_6_out), .sel(tx_data_reg_q_2[23]));
  and and_8 (and_8_out, ~seq_count_q[0], seq_count_q[1], seq_count_q[2], seq_count_q[3], seq_count_q[4]);  // AND_Gate
  Multiplexer #(.width(8)) multiplexer_7 (
    .in0({8{1'b0}}), .in1({{6{1'b0}}, write_busy_q}), .out(rd_data), .sel(addr[2]));
  Comparator #(.mode("unsigned"), .width(5)) comparator_1 (
    .a(seq_count_q), .b(multiplexer_5_out), .eq(comparator_1_eq));  // open: gt, lt
  and and_9 (and_9_out, write_busy_q[0], comparator_1_eq);
  and and_10 (and_10_out, ~and_7_out, not_3_out);  // AND_Gate
  not not_3 (not_3_out, fast_led_out);
  or or_7 (or_7_out, and_9_out, and_7_out);
  Register #(.width(1)) register_1 (.D(and_10_out), .en(or_7_out), .clk(clk), .Q(fast_led_out), .clr(rst));

  // Other names for the same wires on the sheet: c = clk; r = rst
endmodule

module i2c (
  input  clk,
  input  rst,
  input  slave_en,
  input  read_en,
  input  [1:0] addr,
  input  [15:0] write_data,
  input  write_en,
  output [15:0] rd_data,
  output read_resp,
  output tx
);

  wire and_1_out, and_2_out, and_3_out, and_4_out, and_5_out, and_6_out, and_7_out, and_8_out, and_9_out,
       comparator_1_eq, decoder_1_out0, decoder_1_out2, multiplexer_3_out, multiplexer_5_out, nor_1_out,
       not_1_out, or_1_out, or_2_out, or_3_out, register_1_q, register_2_q, xor_1_out;
  wire [0:0] undriven;
  wire [3:0] adder_2_out, multiplexer_4_out, tx_state_reg_q;
  wire [7:0] multiplexer_2_out, tx_data_reg_q;
  wire [15:0] multiplexer_7_out, prescaler_reg_q;
  wire [19:0] adder_1_out, multiplexer_1_out, prescaler_counter_q;

  and and_1 (and_1_out, slave_en, read_en);
  and and_2 (and_2_out, slave_en, write_en);
  Decoder #(.enable("false"), .select(2)) decoder_1 (
    .out0(decoder_1_out0), .out2(decoder_1_out2), .sel(addr));  // open: out1, out3
  and and_3 (and_3_out, decoder_1_out2, and_2_out);
  Adder #(.width(20)) adder_1 (.a(prescaler_counter_q), .b(20'h1), .out(adder_1_out), .cin(1'b0));  // open: cout
  and and_4 (and_4_out, decoder_1_out0, and_2_out);
  Multiplexer #(.width(20)) multiplexer_1 (
    .in0(adder_1_out), .in1({20{1'b0}}), .out(multiplexer_1_out), .sel(or_1_out));
  or or_1 (or_1_out, and_9_out, comparator_1_eq);
  Multiplexer #(.width(8)) multiplexer_2 (
    .in0({1'b0, tx_data_reg_q[7:1]}), .in1(write_data[7:0]), .out(multiplexer_2_out), .sel(and_3_out));
  Register #(.width(20)) prescaler_counter (
    .D(multiplexer_1_out), .en(or_2_out), .clk(clk), .Q(prescaler_counter_q), .clr(rst));
  or or_2 (or_2_out, undriven[0], and_9_out, comparator_1_eq);
  Register #(.width(16)) prescaler_reg (.D(write_data), .en(and_4_out), .clk(clk), .Q(prescaler_reg_q), .clr(rst));
  and and_5 (and_5_out, xor_1_out, undriven[0]);
  Multiplexer multiplexer_3 (.in0(xor_1_out), .in1(and_3_out), .out(multiplexer_3_out), .sel(and_6_out));
  or or_3 (or_3_out, and_5_out, and_9_out);
  Register tx_data_reg (.D(multiplexer_2_out), .en(multiplexer_3_out), .clk(clk), .Q(tx_data_reg_q), .clr(rst));
  Adder #(.width(4)) adder_2 (.a(tx_state_reg_q), .b(4'b0001), .out(adder_2_out), .cin(1'b0));  // open: cout
  Multiplexer #(.width(4)) multiplexer_4 (.in0(adder_2_out), .in1(4'b0000), .out(multiplexer_4_out), .sel(and_9_out));
  Comparator #(.mode("unsigned"), .width(20)) comparator_1 (
    .a(prescaler_counter_q), .b({prescaler_reg_q, 4'b0000}), .eq(comparator_1_eq));  // open: gt, lt
  Register #(.width(4)) tx_state_reg (.D(multiplexer_4_out), .en(or_3_out), .clk(clk), .Q(tx_state_reg_q), .clr(rst));
  Register #(.width(1)) register_1 (.D(not_1_out), .en(comparator_1_eq), .clk(clk), .Q(register_1_q), .clr(rst));
  Multiplexer multiplexer_5 (.in0(1'b1), .in1(1'b0), .out(multiplexer_5_out), .sel(and_7_out));
  Multiplexer multiplexer_6 (.in0(multiplexer_5_out), .in1(tx_data_reg_q[0]), .out(tx), .sel(nor_1_out));
  not not_1 (not_1_out, register_1_q);
  Register #(.width(1)) register_2 (.D(not_1_out), .en(undriven[0]), .clk(clk), .Q(register_2_q), .clr(rst));
  nor nor_1 (nor_1_out, and_6_out, and_7_out, and_8_out, and_9_out);
  and and_6 (and_6_out, ~tx_state_reg_q[0], ~tx_state_reg_q[1], ~tx_state_reg_q[2], ~tx_state_reg_q[3]);  // AND_Gate
  and and_7 (and_7_out, tx_state_reg_q[0], ~tx_state_reg_q[1], ~tx_state_reg_q[2], ~tx_state_reg_q[3]);  // AND_Gate
  and and_8 (and_8_out, ~tx_state_reg_q[0], tx_state_reg_q[1], ~tx_state_reg_q[2], tx_state_reg_q[3]);  // AND_Gate
  and and_9 (and_9_out, tx_state_reg_q[0], tx_state_reg_q[1], ~tx_state_reg_q[2], tx_state_reg_q[3]);  // AND_Gate
  xor xor_1 (xor_1_out, not_1_out, register_2_q);
  Multiplexer #(.select(2), .width(16)) multiplexer_7 (
    .in0(prescaler_reg_q), .in1({16{1'b0}}), .in2({16{1'b0}}), .in3({{15{1'b0}}, undriven[0]}),
    .out(multiplexer_7_out), .sel(addr));
  Register #(.width(16)) register_3 (.D(multiplexer_7_out), .en(and_1_out), .clk(clk), .Q(rd_data), .clr(rst));
  Register #(.width(1)) register_4 (.D(and_1_out), .en(1'b1), .clk(clk), .Q(read_resp), .clr(rst));

  // Other names for the same wires on the sheet: c = clk; r = rst
endmodule

module memory (
  input  [31:0] data_in,
  input  [13:0] addr,
  input  slave_en,
  input  wr_en,
  input  [2:0] strobe,
  input  clk,
  output [31:0] data_out
);

  wire and_1_out, and_2_out, and_3_out, and_4_out, and_5_out, not_1_out;
  wire [1:1] decoder_2_out0, decoder_2_out1;
  wire [3:0] decoder_1_out0, multiplexer_1_out;
  wire [7:0] multiplexer_3_out;
  wire [15:0] bank0_dout, bank2_dout, multiplexer_2_out;
  wire [31:0] shifter_1_out, zero_sign_extend_8_1_outp, zero_sign_extend_16_1_outp;

  Shifter #(.width(32)) shifter_1 (.in(data_in), .\dist ({addr[1:0], 3'b000}), .out(shifter_1_out));
  and and_1 (and_1_out, slave_en, wr_en);
  RAM #(.addrWidth(12), .asyncread("true")) bank3 (
    .addr(addr[13:2]), .we(and_2_out), .oe(1'b1), .clk(clk), .din(shifter_1_out[31:24]),
    .dout(bank2_dout[15:8]));
  Decoder #(.enable("false"), .select(2)) decoder_1 (
    .out0(decoder_1_out0[0]), .out1(decoder_1_out0[1]), .out2(decoder_1_out0[2]), .out3(decoder_1_out0[3]),
    .sel(addr[1:0]));
  Decoder #(.enable("false")) decoder_2 (.out0(decoder_2_out0[1]), .out1(decoder_2_out1[1]), .sel(addr[1]));
  and and_2 (and_2_out, and_1_out, multiplexer_1_out[3]);
  Multiplexer #(.select(2), .width(4)) multiplexer_1 (
    .in0(decoder_1_out0), .in1({{2{decoder_2_out1[1]}}, {2{decoder_2_out0[1]}}}), .in2(4'b1111),
    .in3(4'b0000), .out(multiplexer_1_out), .sel(strobe[1:0]));
  RAM #(.addrWidth(12), .asyncread("true")) bank2 (
    .addr(addr[13:2]), .we(and_3_out), .oe(1'b1), .clk(clk), .din(shifter_1_out[23:16]),
    .dout(bank2_dout[7:0]));
  not not_1 (not_1_out, strobe[2]);
  and and_3 (and_3_out, and_1_out, multiplexer_1_out[2]);
  Multiplexer #(.width(16)) multiplexer_2 (.in0(bank0_dout), .in1(bank2_dout), .out(multiplexer_2_out), .sel(addr[1]));
  Multiplexer #(.select(2), .width(8)) multiplexer_3 (
    .in0(bank0_dout[7:0]), .in1(bank0_dout[15:8]), .in2(bank2_dout[7:0]), .in3(bank2_dout[15:8]),
    .out(multiplexer_3_out), .sel(addr[1:0]));
  RAM #(.addrWidth(12), .asyncread("true")) bank1 (
    .addr(addr[13:2]), .we(and_4_out), .oe(1'b1), .clk(clk), .din(shifter_1_out[15:8]),
    .dout(bank0_dout[15:8]));
  and and_4 (and_4_out, and_1_out, multiplexer_1_out[1]);
  zero_sign_extend_16 zero_sign_extend_16_1 (
    .inpt(multiplexer_2_out), .sign_ext_en(not_1_out), .outp(zero_sign_extend_16_1_outp));
  zero_sign_extend_8 zero_sign_extend_8_1 (
    .inpt(multiplexer_3_out), .sign_ext_en(not_1_out), .outp(zero_sign_extend_8_1_outp));
  Multiplexer #(.select(2), .width(32)) multiplexer_4 (
    .in0(zero_sign_extend_8_1_outp), .in1(zero_sign_extend_16_1_outp), .in2({bank2_dout, bank0_dout}),
    .in3({32{1'b0}}), .out(data_out), .sel(strobe[1:0]));
  // Probe on data_out
  RAM #(.addrWidth(12), .asyncread("true")) bank0 (
    .addr(addr[13:2]), .we(and_5_out), .oe(1'b1), .clk(clk), .din(shifter_1_out[7:0]), .dout(bank0_dout[7:0]));
  and and_5 (and_5_out, and_1_out, multiplexer_1_out[0]);
endmodule

module memory_rtl_synth (
  input  [31:0] data_in,
  input  [13:0] addr,
  input  slave_en,
  input  wr_en,
  input  [2:0] strobe,
  input  clk,
  output [31:0] data_out
);

  wire and_1_out, and_2_out, and_3_out, and_4_out, and_5_out;
  wire [1:1] decoder_2_out0, decoder_2_out1;
  wire [3:0] decoder_1_out0, multiplexer_1_out;
  wire [7:0] multiplexer_3_out;
  wire [15:0] bram_bank_0_do, bram_bank_2_do, multiplexer_2_out;
  wire [31:0] shifter_1_out, zero_sign_extend_8_1_outp, zero_sign_extend_16_1_outp;

  Shifter #(.width(32)) shifter_1 (.in(data_in), .\dist ({addr[1:0], 3'b000}), .out(shifter_1_out));
  and and_1 (and_1_out, slave_en, wr_en);
  Decoder #(.enable("false"), .select(2)) decoder_1 (
    .out0(decoder_1_out0[0]), .out1(decoder_1_out0[1]), .out2(decoder_1_out0[2]), .out3(decoder_1_out0[3]),
    .sel(addr[1:0]));
  Decoder #(.enable("false")) decoder_2 (.out0(decoder_2_out0[1]), .out1(decoder_2_out1[1]), .sel(addr[1]));
  and and_2 (and_2_out, and_1_out, multiplexer_1_out[3]);
  bram_place_holder bram_bank_3 (
    .A(addr[13:2]), .WE(and_2_out), .clk(clk), .DI(shifter_1_out[31:24]), .DO(bram_bank_2_do[15:8]));
  Multiplexer #(.select(2), .width(4)) multiplexer_1 (
    .in0(decoder_1_out0), .in1({{2{decoder_2_out1[1]}}, {2{decoder_2_out0[1]}}}), .in2(4'b1111),
    .in3(4'b0000), .out(multiplexer_1_out), .sel(strobe[1:0]));
  and and_3 (and_3_out, and_1_out, multiplexer_1_out[2]);
  bram_place_holder bram_bank_2 (
    .A(addr[13:2]), .WE(and_3_out), .clk(clk), .DI(shifter_1_out[23:16]), .DO(bram_bank_2_do[7:0]));
  Multiplexer #(.width(16)) multiplexer_2 (
    .in0(bram_bank_0_do), .in1(bram_bank_2_do), .out(multiplexer_2_out), .sel(addr[1]));
  Multiplexer #(.select(2), .width(8)) multiplexer_3 (
    .in0(bram_bank_0_do[7:0]), .in1(bram_bank_0_do[15:8]), .in2(bram_bank_2_do[7:0]),
    .in3(bram_bank_2_do[15:8]), .out(multiplexer_3_out), .sel(addr[1:0]));
  and and_4 (and_4_out, and_1_out, multiplexer_1_out[1]);
  zero_sign_extend_16 zero_sign_extend_16_1 (
    .inpt(multiplexer_2_out), .sign_ext_en(strobe[2]), .outp(zero_sign_extend_16_1_outp));
  bram_place_holder bram_bank_1 (
    .A(addr[13:2]), .WE(and_4_out), .clk(clk), .DI(shifter_1_out[15:8]), .DO(bram_bank_0_do[15:8]));
  zero_sign_extend_8 zero_sign_extend_8_1 (
    .inpt(multiplexer_3_out), .sign_ext_en(strobe[2]), .outp(zero_sign_extend_8_1_outp));
  Multiplexer #(.select(2), .width(32)) multiplexer_4 (
    .in0(zero_sign_extend_8_1_outp), .in1(zero_sign_extend_16_1_outp),
    .in2({bram_bank_2_do, bram_bank_0_do}), .in3({32{1'b0}}), .out(data_out), .sel(strobe[1:0]));
  // Probe on data_out
  and and_5 (and_5_out, and_1_out, multiplexer_1_out[0]);
  bram_place_holder bram_bank_0 (
    .A(addr[13:2]), .WE(and_5_out), .clk(clk), .DI(shifter_1_out[7:0]), .DO(bram_bank_0_do[7:0]));
endmodule

module bram_place_holder (
  input  [11:0] A,
  input  WE,
  input  clk,
  input  [7:0] DI,
  output [7:0] DO
);


  assign DO = {8{1'b0}};
endmodule

module zero_sign_extend_8 (
  input  [7:0] inpt,
  input  sign_ext_en,
  output [31:0] outp
);

  and and_1 (outp[31], inpt[7], sign_ext_en);

  assign outp[30:0] = {{23{outp[31]}}, inpt};
endmodule

module zero_sign_extend_16 (
  input  [15:0] inpt,
  input  sign_ext_en,
  output [31:0] outp
);

  and and_1 (outp[31], inpt[15], sign_ext_en);

  assign outp[30:0] = {{15{outp[31]}}, inpt};
endmodule

module zero_detection (
  input  [31:0] data,
  output ZERO
);

  nor nor_1 (ZERO, data[0], data[1], data[2], data[3], data[4], data[5], data[6], data[7], data[8], data[9], data[10], data[11], data[12], data[13], data[14], data[15], data[16], data[17], data[18], data[19], data[20], data[21], data[22], data[23], data[24], data[25], data[26], data[27], data[28], data[29], data[30], data[31]);
endmodule

module alu_v2 (
  input  [31:0] a_input,
  input  [31:0] b_input,
  input  func_7,
  input  [2:0] func_3,
  output ZERO,
  output [31:0] ALU_OUT
);

  wire adder_v1_1_slt, adder_v1_1_sltu, not_1_out, not_2_out, or_2_out, undriven;
  wire [0:0] and_2_out, and_3_out;
  wire [31:0] adder_v1_1_sum, and_1_out, multiplexer_1_out, or_1_out, shifter_1_out, shifter_2_out,
       shifter_3_out, xor_1_out;

  // Probe on a_input
  // Probe on a_input
  // Probe on a_input
  Shifter #(.shift("lr"), .width(32)) shifter_1 (.in(a_input), .\dist (b_input[4:0]), .out(shifter_1_out));
  Shifter #(.shift("ar"), .width(32)) shifter_2 (.in(a_input), .\dist (b_input[4:0]), .out(shifter_2_out));
  // Probe on b_input
  Shifter #(.width(32)) shifter_3 (.in(a_input), .\dist (b_input[4:0]), .out(shifter_3_out));
  assign xor_1_out = b_input ^ a_input;  // XOR_Gate xor_1, 32 bits wide
  assign or_1_out = a_input | b_input;  // OR_Gate or_1, 32 bits wide
  assign and_1_out = a_input & b_input;  // AND_Gate and_1, 32 bits wide
  // Probe on b_input
  // Probe on b_input
  adder_v1 adder_v1_1 (
    .func7(func_7), .a(a_input), .b(b_input), .sum(adder_v1_1_sum), .slt(adder_v1_1_slt),
    .sltu(adder_v1_1_sltu));
  not not_1 (not_1_out, adder_v1_1_sltu);
  not not_2 (not_2_out, undriven);
  Multiplexer #(.width(32)) multiplexer_1 (
    .in0(shifter_1_out), .in1(shifter_2_out), .out(multiplexer_1_out), .sel(func_7));
  and and_2 (and_2_out[0], adder_v1_1_sum[31], not_1_out);
  or or_2 (or_2_out, adder_v1_1_sum[31], adder_v1_1_slt);
  and and_3 (and_3_out[0], or_2_out, not_2_out);
  // Probe on adder_v1_1_sum
  // Probe on adder_v1_1_sum
  Multiplexer #(.select(3), .width(32)) multiplexer_2 (
    .in0(adder_v1_1_sum), .in1(shifter_3_out), .in2({{31{1'b0}}, and_2_out[0]}),
    .in3({{31{1'b0}}, and_3_out[0]}), .in4(xor_1_out), .in5(multiplexer_1_out), .in6(or_1_out),
    .in7(and_1_out), .out(ALU_OUT), .sel(func_3));
  nor nor_1 (ZERO, ALU_OUT[0], ALU_OUT[1], ALU_OUT[2], ALU_OUT[3], ALU_OUT[4], ALU_OUT[5], ALU_OUT[6], ALU_OUT[7], ALU_OUT[8], ALU_OUT[9], ALU_OUT[10], ALU_OUT[11], ALU_OUT[12], ALU_OUT[13], ALU_OUT[14], ALU_OUT[15], ALU_OUT[16], ALU_OUT[17], ALU_OUT[18], ALU_OUT[19], ALU_OUT[20], ALU_OUT[21], ALU_OUT[22], ALU_OUT[23], ALU_OUT[24], ALU_OUT[25], ALU_OUT[26], ALU_OUT[27], ALU_OUT[28], ALU_OUT[29], ALU_OUT[30], ALU_OUT[31]);

  // Notes on the sheet:
  //   1). 001 --> SLL
  //   4). 100 --> XOR
  //   6). 110 --> OR
  //   7). 111 --> AND
  //   0). 000 --> ADD/SUB, 2). 010 --> SLT
  //   3). 011 --> SLTU, unsigned ADD/SUB
  //   5). 101 --> SRL/SRA
endmodule

module adder_v1 (
  input  func7,
  input  [31:0] a,
  input  [31:0] b,
  output [31:0] sum,
  output slt,
  output sltu
);

  wire adder_1_cout, adder_2_cout, xor_1_out;
  wire [31:0] multiplexer_1_out, not_1_out;

  // Probe on b
  // Probe on b
  // Probe on a
  // Probe on a
  assign not_1_out = ~b;  // NOT_Gate not_1, 32 bits wide
  Multiplexer #(.width(32)) multiplexer_1 (.in0(b), .in1(not_1_out), .out(multiplexer_1_out), .sel(func7));
  Adder #(.width(31)) adder_1 (
    .a(a[30:0]), .b(multiplexer_1_out[30:0]), .out(sum[30:0]), .cin(func7), .cout(adder_1_cout));
  Adder #(.width(1)) adder_2 (
    .a(a[31]), .b(multiplexer_1_out[31]), .out(sum[31]), .cin(adder_1_cout), .cout(adder_2_cout));
  xor xor_1 (xor_1_out, adder_1_cout, adder_2_cout);
  not not_2 (sltu, adder_2_cout);
  // Probe on sum
  // Probe on sum
  xor xor_2 (slt, sum[31], xor_1_out);
endmodule

module adder_v1_test (
  input  [31:0] a,
  input  func7,
  input  [31:0] b,
  input  in_4,
  input  in_5,
  input  in_6,
  output [31:0] sum,
  output slt,
  output sltu
);

  wire adder_1_cout, adder_2_cout, and_1_out, clock_1_out, comparator_1_lt, comparator_2_lt,
       controlled_buffer_1_out, xnor_1_out, xnor_2_out, xor_1_out;
  wire [30:0] register_1_q;
  wire [31:0] multiplexer_1_out, not_1_out, random_1_out, random_2_out, register_2_q;
  wire [31:31] register_1_q_2;

  Random #(.width(32)) random_1 (.clr(in_4), .next(and_1_out), .clk(controlled_buffer_1_out), .out(random_1_out));
  Random #(.width(32)) random_2 (.clr(in_6), .next(and_1_out), .clk(controlled_buffer_1_out), .out(random_2_out));
  Register #(.width(32)) register_1 (
    .D(random_1_out), .en(and_1_out), .clk(controlled_buffer_1_out), .Q({register_1_q_2[31], register_1_q}),
    .clr(in_5));
  Register #(.width(32)) register_2 (
    .D(random_2_out), .en(and_1_out), .clk(controlled_buffer_1_out), .Q(register_2_q), .clr(in_5));
  assign controlled_buffer_1_out = and_1_out ? clock_1_out : 1'bz;  // Controlled_Buffer controlled_buffer_1
  Clock clock_1 (.out(clock_1_out));
  and and_1 (and_1_out, xnor_1_out, xnor_2_out);
  // Probe on register_2_q
  // Probe on register_2_q
  // Probe on {register_1_q_2[31], register_1_q}
  // Probe on {register_1_q_2[31], register_1_q}
  assign not_1_out = ~register_2_q;  // NOT_Gate not_1, 32 bits wide
  Multiplexer #(.width(32)) multiplexer_1 (.in0(register_2_q), .in1(not_1_out), .out(multiplexer_1_out), .sel(func7));
  Comparator #(.mode("unsigned"), .width(32)) comparator_1 (
    .a({register_1_q_2[31], register_1_q}), .b(register_2_q), .lt(comparator_1_lt));  // open: gt, eq
  Adder #(.width(31)) adder_1 (
    .a(register_1_q), .b(multiplexer_1_out[30:0]), .out(sum[30:0]), .cin(func7), .cout(adder_1_cout));
  Adder #(.width(1)) adder_2 (
    .a(register_1_q_2[31]), .b(multiplexer_1_out[31]), .out(sum[31]), .cin(adder_1_cout), .cout(adder_2_cout));
  Comparator #(.width(32)) comparator_2 (
    .a({register_1_q_2[31], register_1_q}), .b(register_2_q), .lt(comparator_2_lt));  // open: gt, eq
  xor xor_1 (xor_1_out, adder_1_cout, adder_2_cout);
  not not_2 (sltu, adder_2_cout);
  xnor xnor_1 (xnor_1_out, sltu, comparator_1_lt);
  // Probe on sum
  // Probe on sum
  xor xor_2 (slt, sum[31], xor_1_out);
  xnor xnor_2 (xnor_2_out, slt, comparator_2_lt);
endmodule

module clock_divider_by2 (
  input  clk_in,
  input  rst,
  output clk_out
);

  wire not_1_out;

  Register #(.width(1)) register_1 (.D(not_1_out), .en(1'b1), .clk(clk_in), .Q(clk_out), .clr(rst));
  not not_1 (not_1_out, clk_out);
endmodule

module reset_synchronizer (
  input  clk,
  input  rst_in,
  output rst_out
);

  wire register_1_q;

  Register #(.width(1)) register_1 (.D(1'b1), .en(1'b1), .clk(clk), .Q(register_1_q), .clr(rst_in));
  Register #(.width(1)) register_2 (.D(register_1_q), .en(1'b1), .clk(clk), .Q(rst_out), .clr(rst_in));
endmodule

module gpio_buffer (
  input  [19:0] data_in,
  input  [19:0] data_en,
  output [19:0] data_out
);

  assign data_out[0] = data_en[0] ? data_in[0] : 1'bz;  // Controlled_Buffer controlled_buffer_1
  assign data_out[1] = data_en[1] ? data_in[1] : 1'bz;  // Controlled_Buffer controlled_buffer_2
  assign data_out[2] = data_en[2] ? data_in[2] : 1'bz;  // Controlled_Buffer controlled_buffer_3
  assign data_out[3] = data_en[3] ? data_in[3] : 1'bz;  // Controlled_Buffer controlled_buffer_4
  assign data_out[4] = data_en[4] ? data_in[4] : 1'bz;  // Controlled_Buffer controlled_buffer_5
  assign data_out[5] = data_en[5] ? data_in[5] : 1'bz;  // Controlled_Buffer controlled_buffer_6
  assign data_out[6] = data_en[6] ? data_in[6] : 1'bz;  // Controlled_Buffer controlled_buffer_7
  assign data_out[7] = data_en[7] ? data_in[7] : 1'bz;  // Controlled_Buffer controlled_buffer_8
  assign data_out[8] = data_en[8] ? data_in[8] : 1'bz;  // Controlled_Buffer controlled_buffer_9
  assign data_out[9] = data_en[9] ? data_in[9] : 1'bz;  // Controlled_Buffer controlled_buffer_10
  assign data_out[10] = data_en[10] ? data_in[10] : 1'bz;  // Controlled_Buffer controlled_buffer_11
  assign data_out[11] = data_en[11] ? data_in[11] : 1'bz;  // Controlled_Buffer controlled_buffer_12
  assign data_out[12] = data_en[12] ? data_in[12] : 1'bz;  // Controlled_Buffer controlled_buffer_13
  assign data_out[13] = data_en[13] ? data_in[13] : 1'bz;  // Controlled_Buffer controlled_buffer_14
  assign data_out[14] = data_en[14] ? data_in[14] : 1'bz;  // Controlled_Buffer controlled_buffer_15
  assign data_out[15] = data_en[15] ? data_in[15] : 1'bz;  // Controlled_Buffer controlled_buffer_16
  assign data_out[16] = data_en[16] ? data_in[16] : 1'bz;  // Controlled_Buffer controlled_buffer_17
  assign data_out[17] = data_en[17] ? data_in[17] : 1'bz;  // Controlled_Buffer controlled_buffer_18
  assign data_out[18] = data_en[18] ? data_in[18] : 1'bz;  // Controlled_Buffer controlled_buffer_19
  assign data_out[19] = data_en[19] ? data_in[19] : 1'bz;  // Controlled_Buffer controlled_buffer_20
endmodule

module inter_stage_buffer (
  input  [31:0] in_1,
  input  [31:0] in_2,
  input  rdy_stall,
  input  [31:0] in_4,
  input  [31:0] in_5,
  input  [2:0] funct3_in,
  input  [6:0] funct7_in,
  input  [3:0] inst_encoded_s1,
  input  clk,
  input  rst,
  output [31:0] out_11,
  output [31:0] out_12,
  output [31:0] out_13,
  output [31:0] out_14,
  output [2:0] funct3_out,
  output [6:0] funct7_out,
  output [3:0] inst_encoded_s2
);

  Register #(.width(32)) register_1 (.D(in_1), .en(rdy_stall), .clk(clk), .Q(out_11), .clr(rst));
  Register #(.width(32)) register_2 (.D(in_2), .en(rdy_stall), .clk(clk), .Q(out_12), .clr(rst));
  Register #(.width(32)) register_3 (.D(in_4), .en(rdy_stall), .clk(clk), .Q(out_13), .clr(rst));
  Register #(.width(32)) register_4 (.D(in_5), .en(rdy_stall), .clk(clk), .Q(out_14), .clr(rst));
  Register #(.width(3)) register_5 (.D(funct3_in), .en(rdy_stall), .clk(clk), .Q(funct3_out), .clr(rst));
  Register #(.width(7)) register_6 (.D(funct7_in), .en(rdy_stall), .clk(clk), .Q(funct7_out), .clr(rst));
  Register #(.width(4)) register_7 (.D(inst_encoded_s1), .en(rdy_stall), .clk(clk), .Q(inst_encoded_s2), .clr(rst));
endmodule

module op_fwd_check (
  input  [4:0] S2_prev_rd,
  input  prev_rd_in,
  input  clk,
  input  rst,
  input  [4:0] curr_rs1,
  input  [4:0] curr_rs2,
  input  rd_fwd_disable,
  input  [1:0] rs1_rs2_fwd_disable,
  output [4:0] rd_stage2,
  output rs1_s2_dep_detected,
  output rs2_s2_dep_detected,
  output rs2_store_fwd,
  output rs1_s1_dep_detected
);

  wire and_1_out, and_2_out, and_3_out, and_4_out, nand_1_out, nand_2_out, nor_1_out, nor_2_out, nor_3_out,
       register_2_q, register_3_q, register_4_q;
  wire [1:0] not_1_out, register_5_q;
  wire [4:0] xnor_1_out, xnor_2_out;

  Register #(.width(5)) register_1 (.D(S2_prev_rd), .en(prev_rd_in), .clk(clk), .Q(rd_stage2), .clr(rst));
  assign xnor_1_out = ~(rd_stage2 ^ curr_rs2);  // XNOR_Gate xnor_1, 5 bits wide
  nor nor_1 (nor_1_out, curr_rs1[0], curr_rs1[1], curr_rs1[2], curr_rs1[3], curr_rs1[4]);
  nor nor_2 (nor_2_out, curr_rs2[0], curr_rs2[1], curr_rs2[2], curr_rs2[3], curr_rs2[4]);
  assign not_1_out = ~rs1_rs2_fwd_disable;  // NOT_Gate not_1, 2 bits wide
  nor nor_3 (nor_3_out, rd_stage2[0], rd_stage2[1], rd_stage2[2], rd_stage2[3], rd_stage2[4]);
  assign xnor_2_out = ~(rd_stage2 ^ curr_rs1);  // XNOR_Gate xnor_2, 5 bits wide
  and and_1 (and_1_out, xnor_2_out[0], xnor_2_out[1], xnor_2_out[2], xnor_2_out[3], xnor_2_out[4]);
  and and_2 (and_2_out, xnor_1_out[0], xnor_1_out[1], xnor_1_out[2], xnor_1_out[3], xnor_1_out[4]);
  nand nand_1 (nand_1_out, nor_3_out, nor_2_out);
  nand nand_2 (nand_2_out, nor_3_out, nor_1_out);
  and and_3 (and_3_out, and_2_out, nand_1_out);
  and and_4 (and_4_out, nand_2_out, and_1_out);
  Register #(.width(1)) register_2 (.D(and_4_out), .en(1'b1), .clk(clk), .Q(register_2_q), .clr(rst));
  Register #(.width(1)) register_3 (.D(and_3_out), .en(1'b1), .clk(clk), .Q(register_3_q), .clr(rst));
  Register #(.width(1)) register_4 (.D(rd_fwd_disable), .en(1'b1), .clk(clk), .Q(register_4_q), .clr(rst));
  Register #(.width(2)) register_5 (.D(not_1_out), .en(1'b1), .clk(clk), .Q(register_5_q), .clr(rst));
  and and_5 (rs1_s2_dep_detected, register_2_q, register_5_q[0], register_4_q);
  and and_6 (rs2_store_fwd, register_3_q, register_4_q);
  and and_7 (rs1_s1_dep_detected, rd_fwd_disable, and_4_out);
  and and_8 (rs2_s2_dep_detected, rs2_store_fwd, register_5_q[1]);

  // Notes on the sheet:
  //   why seprate fwd signal for store because rs2 alu port is engage/busy for immidiate rs1 + imm_i
  //   why seprate fwd signal for store because rs2 alu port is engage/busy for immidiate rs1 + imm_i
endmodule

module op_fwd_logic_V2 (
  input  [4:0] s2_prev_rd,
  input  [4:0] s1_curr_rs1,
  input  [4:0] s1_curr_rs2,
  output [4:0] rd_stage2,
  output s2_rs1_dep,
  output s2_rs2_dep
);

  wire and_1_out, and_2_out, nand_1_out, nand_2_out, nor_1_out, nor_2_out, nor_3_out;
  wire [4:0] xnor_1_out, xnor_2_out;

  assign xnor_1_out = ~(s2_prev_rd ^ s1_curr_rs2);  // XNOR_Gate xnor_1, 5 bits wide
  nor nor_1 (nor_1_out, s1_curr_rs1[0], s1_curr_rs1[1], s1_curr_rs1[2], s1_curr_rs1[3], s1_curr_rs1[4]);
  nor nor_2 (nor_2_out, s1_curr_rs2[0], s1_curr_rs2[1], s1_curr_rs2[2], s1_curr_rs2[3], s1_curr_rs2[4]);
  nor nor_3 (nor_3_out, s2_prev_rd[0], s2_prev_rd[1], s2_prev_rd[2], s2_prev_rd[3], s2_prev_rd[4]);
  assign xnor_2_out = ~(s2_prev_rd ^ s1_curr_rs1);  // XNOR_Gate xnor_2, 5 bits wide
  and and_1 (and_1_out, xnor_2_out[0], xnor_2_out[1], xnor_2_out[2], xnor_2_out[3], xnor_2_out[4]);
  and and_2 (and_2_out, xnor_1_out[0], xnor_1_out[1], xnor_1_out[2], xnor_1_out[3], xnor_1_out[4]);
  nand nand_1 (nand_1_out, nor_3_out, nor_2_out);
  nand nand_2 (nand_2_out, nor_3_out, nor_1_out);
  and and_3 (s2_rs2_dep, and_2_out, nand_1_out);
  and and_4 (s2_rs1_dep, nand_2_out, and_1_out);

  assign rd_stage2 = s2_prev_rd;

  // Notes on the sheet:
  //   why seprate fwd signal for store because rs2 alu port is engage/busy for immidiate rs1 + imm_i
  //   why seprate fwd signal for store because rs2 alu port is engage/busy for immidiate rs1 + imm_i
endmodule
module dep_check (
  input  [4:0] rd,
  input  [4:0] rs1,
  input  [4:0] rs2,
  output dep_detected
);

  wire comparator_1_eq, comparator_2_eq, or_1_out, or_2_out;

  or or_1 (or_1_out, rd[0], rd[1], rd[2], rd[3], rd[4]);
  Comparator #(.width(5)) comparator_1 (.a(rd), .b(rs1), .eq(comparator_1_eq));  // open: gt, lt
  Comparator #(.width(5)) comparator_2 (.a(rd), .b(rs2), .eq(comparator_2_eq));  // open: gt, lt
  or or_2 (or_2_out, comparator_1_eq, comparator_2_eq);
  and and_1 (dep_detected, or_1_out, or_2_out);
endmodule

module compare (
  input  [31:0] reg1,
  input  [31:0] reg2,
  input  [2:0] func3,
  output comp_out
);

  wire comparator_1_eq, comparator_1_gt, comparator_1_lt, comparator_2_eq, comparator_2_gt, comparator_2_lt,
       not_1_out, or_1_out, or_2_out;

  Comparator #(.width(32)) comparator_1 (
    .a(reg1), .b(reg2), .gt(comparator_1_gt), .eq(comparator_1_eq), .lt(comparator_1_lt));
  Comparator #(.mode("unsigned"), .width(32)) comparator_2 (
    .a(reg1), .b(reg2), .gt(comparator_2_gt), .eq(comparator_2_eq), .lt(comparator_2_lt));
  or or_1 (or_1_out, comparator_2_gt, comparator_2_eq);
  or or_2 (or_2_out, comparator_1_gt, comparator_1_eq);
  not not_1 (not_1_out, comparator_1_eq);
  Multiplexer #(.select(3)) multiplexer_1 (
    .in0(comparator_1_eq), .in1(not_1_out), .in2(1'b0), .in3(1'b0), .in4(comparator_1_lt), .in5(or_2_out),
    .in6(comparator_2_lt), .in7(or_1_out), .out(comp_out), .sel(func3));
endmodule

module branch_predictor (
  input  branch_sel,
  input  [5:0] prev_pc,
  input  [5:0] curr_pc,
  input  reset,
  input  clock,
  input  branch_taken,
  output pred_out
);

  wire demultiplexer_1_out0, demultiplexer_1_out1, demultiplexer_1_out2, demultiplexer_1_out3,
       demultiplexer_1_out4, demultiplexer_1_out5, demultiplexer_1_out6, demultiplexer_1_out7,
       demultiplexer_1_out8, demultiplexer_1_out9, demultiplexer_1_out10, demultiplexer_1_out11,
       demultiplexer_1_out12, demultiplexer_1_out13, demultiplexer_1_out14, demultiplexer_1_out15,
       demultiplexer_1_out16, demultiplexer_1_out17, demultiplexer_1_out18, demultiplexer_1_out19,
       demultiplexer_1_out20, demultiplexer_1_out21, demultiplexer_1_out22, demultiplexer_1_out23,
       demultiplexer_1_out24, demultiplexer_1_out25, demultiplexer_1_out26, demultiplexer_1_out27,
       demultiplexer_1_out28, demultiplexer_1_out29, demultiplexer_1_out30, demultiplexer_1_out31,
       demultiplexer_1_out32, demultiplexer_1_out33, demultiplexer_1_out34, demultiplexer_1_out35,
       demultiplexer_1_out36, demultiplexer_1_out37, demultiplexer_1_out38, demultiplexer_1_out39,
       demultiplexer_1_out40, demultiplexer_1_out41, demultiplexer_1_out42, demultiplexer_1_out43,
       demultiplexer_1_out44, demultiplexer_1_out45, demultiplexer_1_out46, demultiplexer_1_out47,
       demultiplexer_1_out48, demultiplexer_1_out49, demultiplexer_1_out50, demultiplexer_1_out51,
       demultiplexer_1_out52, demultiplexer_1_out53, demultiplexer_1_out54, demultiplexer_1_out55,
       demultiplexer_1_out56, demultiplexer_1_out57, demultiplexer_1_out58, demultiplexer_1_out59,
       demultiplexer_1_out60, demultiplexer_1_out61, demultiplexer_1_out62, demultiplexer_1_out63;
  wire [0:0] multiplexer_1_out;
  wire [1:0] counter_1_q, counter_2_q, counter_3_q, counter_4_q, counter_5_q, counter_6_q, counter_7_q,
       counter_8_q, counter_9_q, counter_10_q, counter_11_q, counter_12_q, counter_13_q, counter_14_q,
       counter_15_q, counter_16_q, counter_17_q, counter_18_q, counter_19_q, counter_20_q, counter_21_q,
       counter_22_q, counter_23_q, counter_24_q, counter_25_q, counter_26_q, counter_27_q, counter_28_q,
       counter_29_q, counter_30_q, counter_31_q, counter_32_q, counter_33_q, counter_34_q, counter_35_q,
       counter_36_q, counter_37_q, counter_38_q, counter_39_q, counter_40_q, counter_41_q, counter_42_q,
       counter_43_q, counter_44_q, counter_45_q, counter_46_q, counter_47_q, counter_48_q, counter_49_q,
       counter_50_q, counter_51_q, counter_52_q, counter_53_q, counter_54_q, counter_55_q, counter_56_q,
       counter_57_q, counter_58_q, counter_59_q, counter_60_q, counter_61_q, counter_62_q, counter_63_q,
       counter_64_q;

  Demultiplexer #(.select(6)) demultiplexer_1 (
    .out0(demultiplexer_1_out0), .out1(demultiplexer_1_out1), .out2(demultiplexer_1_out2),
    .out3(demultiplexer_1_out3), .out4(demultiplexer_1_out4), .out5(demultiplexer_1_out5),
    .out6(demultiplexer_1_out6), .out7(demultiplexer_1_out7), .out8(demultiplexer_1_out8),
    .out9(demultiplexer_1_out9), .out10(demultiplexer_1_out10), .out11(demultiplexer_1_out11),
    .out12(demultiplexer_1_out12), .out13(demultiplexer_1_out13), .out14(demultiplexer_1_out14),
    .out15(demultiplexer_1_out15), .out16(demultiplexer_1_out16), .out17(demultiplexer_1_out17),
    .out18(demultiplexer_1_out18), .out19(demultiplexer_1_out19), .out20(demultiplexer_1_out20),
    .out21(demultiplexer_1_out21), .out22(demultiplexer_1_out22), .out23(demultiplexer_1_out23),
    .out24(demultiplexer_1_out24), .out25(demultiplexer_1_out25), .out26(demultiplexer_1_out26),
    .out27(demultiplexer_1_out27), .out28(demultiplexer_1_out28), .out29(demultiplexer_1_out29),
    .out30(demultiplexer_1_out30), .out31(demultiplexer_1_out31), .out32(demultiplexer_1_out32),
    .out33(demultiplexer_1_out33), .out34(demultiplexer_1_out34), .out35(demultiplexer_1_out35),
    .out36(demultiplexer_1_out36), .out37(demultiplexer_1_out37), .out38(demultiplexer_1_out38),
    .out39(demultiplexer_1_out39), .out40(demultiplexer_1_out40), .out41(demultiplexer_1_out41),
    .out42(demultiplexer_1_out42), .out43(demultiplexer_1_out43), .out44(demultiplexer_1_out44),
    .out45(demultiplexer_1_out45), .out46(demultiplexer_1_out46), .out47(demultiplexer_1_out47),
    .out48(demultiplexer_1_out48), .out49(demultiplexer_1_out49), .out50(demultiplexer_1_out50),
    .out51(demultiplexer_1_out51), .out52(demultiplexer_1_out52), .out53(demultiplexer_1_out53),
    .out54(demultiplexer_1_out54), .out55(demultiplexer_1_out55), .out56(demultiplexer_1_out56),
    .out57(demultiplexer_1_out57), .out58(demultiplexer_1_out58), .out59(demultiplexer_1_out59),
    .out60(demultiplexer_1_out60), .out61(demultiplexer_1_out61), .out62(demultiplexer_1_out62),
    .out63(demultiplexer_1_out63), .in(branch_sel), .sel(prev_pc));
  Counter #(.max('h3), .ongoal("stay"), .width(2)) counter_1 (
    .count(demultiplexer_1_out7), .Q(counter_1_q), .up(branch_taken), .clk(clock), .clr(reset));  // open: load, D, carry
  Counter #(.max('h3), .ongoal("stay"), .width(2)) counter_2 (
    .count(demultiplexer_1_out15), .Q(counter_2_q), .up(branch_taken), .clk(clock), .clr(reset));  // open: load, D, carry
  Counter #(.max('h3), .ongoal("stay"), .width(2)) counter_3 (
    .count(demultiplexer_1_out23), .Q(counter_3_q), .up(branch_taken), .clk(clock), .clr(reset));  // open: load, D, carry
  Counter #(.max('h3), .ongoal("stay"), .width(2)) counter_4 (
    .count(demultiplexer_1_out31), .Q(counter_4_q), .up(branch_taken), .clk(clock), .clr(reset));  // open: load, D, carry
  Counter #(.max('h3), .ongoal("stay"), .width(2)) counter_5 (
    .count(demultiplexer_1_out39), .Q(counter_5_q), .up(branch_taken), .clk(clock), .clr(reset));  // open: load, D, carry
  Counter #(.max('h3), .ongoal("stay"), .width(2)) counter_6 (
    .count(demultiplexer_1_out47), .Q(counter_6_q), .up(branch_taken), .clk(clock), .clr(reset));  // open: load, D, carry
  Counter #(.max('h3), .ongoal("stay"), .width(2)) counter_7 (
    .count(demultiplexer_1_out55), .Q(counter_7_q), .up(branch_taken), .clk(clock), .clr(reset));  // open: load, D, carry
  Counter #(.max('h3), .ongoal("stay"), .width(2)) counter_8 (
    .count(demultiplexer_1_out63), .Q(counter_8_q), .up(branch_taken), .clk(clock), .clr(reset));  // open: load, D, carry
  Counter #(.max('h3), .ongoal("stay"), .width(2)) counter_9 (
    .count(demultiplexer_1_out6), .Q(counter_9_q), .up(branch_taken), .clk(clock), .clr(reset));  // open: load, D, carry
  Counter #(.max('h3), .ongoal("stay"), .width(2)) counter_10 (
    .count(demultiplexer_1_out14), .Q(counter_10_q), .up(branch_taken), .clk(clock), .clr(reset));  // open: load, D, carry
  Counter #(.max('h3), .ongoal("stay"), .width(2)) counter_11 (
    .count(demultiplexer_1_out22), .Q(counter_11_q), .up(branch_taken), .clk(clock), .clr(reset));  // open: load, D, carry
  Counter #(.max('h3), .ongoal("stay"), .width(2)) counter_12 (
    .count(demultiplexer_1_out30), .Q(counter_12_q), .up(branch_taken), .clk(clock), .clr(reset));  // open: load, D, carry
  Counter #(.max('h3), .ongoal("stay"), .width(2)) counter_13 (
    .count(demultiplexer_1_out38), .Q(counter_13_q), .up(branch_taken), .clk(clock), .clr(reset));  // open: load, D, carry
  Counter #(.max('h3), .ongoal("stay"), .width(2)) counter_14 (
    .count(demultiplexer_1_out46), .Q(counter_14_q), .up(branch_taken), .clk(clock), .clr(reset));  // open: load, D, carry
  Counter #(.max('h3), .ongoal("stay"), .width(2)) counter_15 (
    .count(demultiplexer_1_out54), .Q(counter_15_q), .up(branch_taken), .clk(clock), .clr(reset));  // open: load, D, carry
  Counter #(.max('h3), .ongoal("stay"), .width(2)) counter_16 (
    .count(demultiplexer_1_out62), .Q(counter_16_q), .up(branch_taken), .clk(clock), .clr(reset));  // open: load, D, carry
  Counter #(.max('h3), .ongoal("stay"), .width(2)) counter_17 (
    .count(demultiplexer_1_out5), .Q(counter_17_q), .up(branch_taken), .clk(clock), .clr(reset));  // open: load, D, carry
  Counter #(.max('h3), .ongoal("stay"), .width(2)) counter_18 (
    .count(demultiplexer_1_out13), .Q(counter_18_q), .up(branch_taken), .clk(clock), .clr(reset));  // open: load, D, carry
  Counter #(.max('h3), .ongoal("stay"), .width(2)) counter_19 (
    .count(demultiplexer_1_out21), .Q(counter_19_q), .up(branch_taken), .clk(clock), .clr(reset));  // open: load, D, carry
  Counter #(.max('h3), .ongoal("stay"), .width(2)) counter_20 (
    .count(demultiplexer_1_out29), .Q(counter_20_q), .up(branch_taken), .clk(clock), .clr(reset));  // open: load, D, carry
  Counter #(.max('h3), .ongoal("stay"), .width(2)) counter_21 (
    .count(demultiplexer_1_out37), .Q(counter_21_q), .up(branch_taken), .clk(clock), .clr(reset));  // open: load, D, carry
  Counter #(.max('h3), .ongoal("stay"), .width(2)) counter_22 (
    .count(demultiplexer_1_out45), .Q(counter_22_q), .up(branch_taken), .clk(clock), .clr(reset));  // open: load, D, carry
  Counter #(.max('h3), .ongoal("stay"), .width(2)) counter_23 (
    .count(demultiplexer_1_out53), .Q(counter_23_q), .up(branch_taken), .clk(clock), .clr(reset));  // open: load, D, carry
  Counter #(.max('h3), .ongoal("stay"), .width(2)) counter_24 (
    .count(demultiplexer_1_out61), .Q(counter_24_q), .up(branch_taken), .clk(clock), .clr(reset));  // open: load, D, carry
  Counter #(.max('h3), .ongoal("stay"), .width(2)) counter_25 (
    .count(demultiplexer_1_out4), .Q(counter_25_q), .up(branch_taken), .clk(clock), .clr(reset));  // open: load, D, carry
  Counter #(.max('h3), .ongoal("stay"), .width(2)) counter_26 (
    .count(demultiplexer_1_out12), .Q(counter_26_q), .up(branch_taken), .clk(clock), .clr(reset));  // open: load, D, carry
  Counter #(.max('h3), .ongoal("stay"), .width(2)) counter_27 (
    .count(demultiplexer_1_out20), .Q(counter_27_q), .up(branch_taken), .clk(clock), .clr(reset));  // open: load, D, carry
  Counter #(.max('h3), .ongoal("stay"), .width(2)) counter_28 (
    .count(demultiplexer_1_out28), .Q(counter_28_q), .up(branch_taken), .clk(clock), .clr(reset));  // open: load, D, carry
  Counter #(.max('h3), .ongoal("stay"), .width(2)) counter_29 (
    .count(demultiplexer_1_out36), .Q(counter_29_q), .up(branch_taken), .clk(clock), .clr(reset));  // open: load, D, carry
  Counter #(.max('h3), .ongoal("stay"), .width(2)) counter_30 (
    .count(demultiplexer_1_out44), .Q(counter_30_q), .up(branch_taken), .clk(clock), .clr(reset));  // open: load, D, carry
  Counter #(.max('h3), .ongoal("stay"), .width(2)) counter_31 (
    .count(demultiplexer_1_out52), .Q(counter_31_q), .up(branch_taken), .clk(clock), .clr(reset));  // open: load, D, carry
  Counter #(.max('h3), .ongoal("stay"), .width(2)) counter_32 (
    .count(demultiplexer_1_out60), .Q(counter_32_q), .up(branch_taken), .clk(clock), .clr(reset));  // open: load, D, carry
  Counter #(.max('h3), .ongoal("stay"), .width(2)) counter_33 (
    .count(demultiplexer_1_out3), .Q(counter_33_q), .up(branch_taken), .clk(clock), .clr(reset));  // open: load, D, carry
  Counter #(.max('h3), .ongoal("stay"), .width(2)) counter_34 (
    .count(demultiplexer_1_out11), .Q(counter_34_q), .up(branch_taken), .clk(clock), .clr(reset));  // open: load, D, carry
  Counter #(.max('h3), .ongoal("stay"), .width(2)) counter_35 (
    .count(demultiplexer_1_out19), .Q(counter_35_q), .up(branch_taken), .clk(clock), .clr(reset));  // open: load, D, carry
  Counter #(.max('h3), .ongoal("stay"), .width(2)) counter_36 (
    .count(demultiplexer_1_out27), .Q(counter_36_q), .up(branch_taken), .clk(clock), .clr(reset));  // open: load, D, carry
  Counter #(.max('h3), .ongoal("stay"), .width(2)) counter_37 (
    .count(demultiplexer_1_out35), .Q(counter_37_q), .up(branch_taken), .clk(clock), .clr(reset));  // open: load, D, carry
  Counter #(.max('h3), .ongoal("stay"), .width(2)) counter_38 (
    .count(demultiplexer_1_out43), .Q(counter_38_q), .up(branch_taken), .clk(clock), .clr(reset));  // open: load, D, carry
  Counter #(.max('h3), .ongoal("stay"), .width(2)) counter_39 (
    .count(demultiplexer_1_out51), .Q(counter_39_q), .up(branch_taken), .clk(clock), .clr(reset));  // open: load, D, carry
  Counter #(.max('h3), .ongoal("stay"), .width(2)) counter_40 (
    .count(demultiplexer_1_out59), .Q(counter_40_q), .up(branch_taken), .clk(clock), .clr(reset));  // open: load, D, carry
  Counter #(.max('h3), .ongoal("stay"), .width(2)) counter_41 (
    .count(demultiplexer_1_out2), .Q(counter_41_q), .up(branch_taken), .clk(clock), .clr(reset));  // open: load, D, carry
  Counter #(.max('h3), .ongoal("stay"), .width(2)) counter_42 (
    .count(demultiplexer_1_out10), .Q(counter_42_q), .up(branch_taken), .clk(clock), .clr(reset));  // open: load, D, carry
  Counter #(.max('h3), .ongoal("stay"), .width(2)) counter_43 (
    .count(demultiplexer_1_out18), .Q(counter_43_q), .up(branch_taken), .clk(clock), .clr(reset));  // open: load, D, carry
  Counter #(.max('h3), .ongoal("stay"), .width(2)) counter_44 (
    .count(demultiplexer_1_out26), .Q(counter_44_q), .up(branch_taken), .clk(clock), .clr(reset));  // open: load, D, carry
  Counter #(.max('h3), .ongoal("stay"), .width(2)) counter_45 (
    .count(demultiplexer_1_out34), .Q(counter_45_q), .up(branch_taken), .clk(clock), .clr(reset));  // open: load, D, carry
  Counter #(.max('h3), .ongoal("stay"), .width(2)) counter_46 (
    .count(demultiplexer_1_out42), .Q(counter_46_q), .up(branch_taken), .clk(clock), .clr(reset));  // open: load, D, carry
  Counter #(.max('h3), .ongoal("stay"), .width(2)) counter_47 (
    .count(demultiplexer_1_out50), .Q(counter_47_q), .up(branch_taken), .clk(clock), .clr(reset));  // open: load, D, carry
  Counter #(.max('h3), .ongoal("stay"), .width(2)) counter_48 (
    .count(demultiplexer_1_out58), .Q(counter_48_q), .up(branch_taken), .clk(clock), .clr(reset));  // open: load, D, carry
  Counter #(.max('h3), .ongoal("stay"), .width(2)) counter_49 (
    .count(demultiplexer_1_out1), .Q(counter_49_q), .up(branch_taken), .clk(clock), .clr(reset));  // open: load, D, carry
  Counter #(.max('h3), .ongoal("stay"), .width(2)) counter_50 (
    .count(demultiplexer_1_out9), .Q(counter_50_q), .up(branch_taken), .clk(clock), .clr(reset));  // open: load, D, carry
  Counter #(.max('h3), .ongoal("stay"), .width(2)) counter_51 (
    .count(demultiplexer_1_out17), .Q(counter_51_q), .up(branch_taken), .clk(clock), .clr(reset));  // open: load, D, carry
  Counter #(.max('h3), .ongoal("stay"), .width(2)) counter_52 (
    .count(demultiplexer_1_out25), .Q(counter_52_q), .up(branch_taken), .clk(clock), .clr(reset));  // open: load, D, carry
  Counter #(.max('h3), .ongoal("stay"), .width(2)) counter_53 (
    .count(demultiplexer_1_out33), .Q(counter_53_q), .up(branch_taken), .clk(clock), .clr(reset));  // open: load, D, carry
  Counter #(.max('h3), .ongoal("stay"), .width(2)) counter_54 (
    .count(demultiplexer_1_out41), .Q(counter_54_q), .up(branch_taken), .clk(clock), .clr(reset));  // open: load, D, carry
  Counter #(.max('h3), .ongoal("stay"), .width(2)) counter_55 (
    .count(demultiplexer_1_out49), .Q(counter_55_q), .up(branch_taken), .clk(clock), .clr(reset));  // open: load, D, carry
  Counter #(.max('h3), .ongoal("stay"), .width(2)) counter_56 (
    .count(demultiplexer_1_out57), .Q(counter_56_q), .up(branch_taken), .clk(clock), .clr(reset));  // open: load, D, carry
  Counter #(.max('h3), .ongoal("stay"), .width(2)) counter_57 (
    .count(demultiplexer_1_out0), .Q(counter_57_q), .up(branch_taken), .clk(clock), .clr(reset));  // open: load, D, carry
  Counter #(.max('h3), .ongoal("stay"), .width(2)) counter_58 (
    .count(demultiplexer_1_out8), .Q(counter_58_q), .up(branch_taken), .clk(clock), .clr(reset));  // open: load, D, carry
  Counter #(.max('h3), .ongoal("stay"), .width(2)) counter_59 (
    .count(demultiplexer_1_out16), .Q(counter_59_q), .up(branch_taken), .clk(clock), .clr(reset));  // open: load, D, carry
  Counter #(.max('h3), .ongoal("stay"), .width(2)) counter_60 (
    .count(demultiplexer_1_out24), .Q(counter_60_q), .up(branch_taken), .clk(clock), .clr(reset));  // open: load, D, carry
  Counter #(.max('h3), .ongoal("stay"), .width(2)) counter_61 (
    .count(demultiplexer_1_out32), .Q(counter_61_q), .up(branch_taken), .clk(clock), .clr(reset));  // open: load, D, carry
  Counter #(.max('h3), .ongoal("stay"), .width(2)) counter_62 (
    .count(demultiplexer_1_out40), .Q(counter_62_q), .up(branch_taken), .clk(clock), .clr(reset));  // open: load, D, carry
  Counter #(.max('h3), .ongoal("stay"), .width(2)) counter_63 (
    .count(demultiplexer_1_out48), .Q(counter_63_q), .up(branch_taken), .clk(clock), .clr(reset));  // open: load, D, carry
  Counter #(.max('h3), .ongoal("stay"), .width(2)) counter_64 (
    .count(demultiplexer_1_out56), .Q(counter_64_q), .up(branch_taken), .clk(clock), .clr(reset));  // open: load, D, carry
  Multiplexer #(.select(6), .width(2)) multiplexer_1 (
    .in0(counter_57_q), .in1(counter_49_q), .in2(counter_41_q), .in3(counter_33_q), .in4(counter_25_q),
    .in5(counter_17_q), .in6(counter_9_q), .in7(counter_1_q), .in8(counter_58_q), .in9(counter_50_q),
    .in10(counter_42_q), .in11(counter_34_q), .in12(counter_26_q), .in13(counter_18_q), .in14(counter_10_q),
    .in15(counter_2_q), .in16(counter_59_q), .in17(counter_51_q), .in18(counter_43_q), .in19(counter_35_q),
    .in20(counter_27_q), .in21(counter_19_q), .in22(counter_11_q), .in23(counter_3_q), .in24(counter_60_q),
    .in25(counter_52_q), .in26(counter_44_q), .in27(counter_36_q), .in28(counter_28_q), .in29(counter_20_q),
    .in30(counter_12_q), .in31(counter_4_q), .in32(counter_61_q), .in33(counter_53_q), .in34(counter_45_q),
    .in35(counter_37_q), .in36(counter_29_q), .in37(counter_21_q), .in38(counter_13_q), .in39(counter_5_q),
    .in40(counter_62_q), .in41(counter_54_q), .in42(counter_46_q), .in43(counter_38_q), .in44(counter_30_q),
    .in45(counter_22_q), .in46(counter_14_q), .in47(counter_6_q), .in48(counter_63_q), .in49(counter_55_q),
    .in50(counter_47_q), .in51(counter_39_q), .in52(counter_31_q), .in53(counter_23_q), .in54(counter_15_q),
    .in55(counter_7_q), .in56(counter_64_q), .in57(counter_56_q), .in58(counter_48_q), .in59(counter_40_q),
    .in60(counter_32_q), .in61(counter_24_q), .in62(counter_16_q), .in63(counter_8_q),
    .out({pred_out, multiplexer_1_out[0]}), .sel(curr_pc));
endmodule
